// Logisim project cpu24.circ as structural Verilog: 17 circuits, main circuit ◇理想流水线
module \理想流水线  (
  output [31:0] out_1
);

  wire AluSrcB, and_1_out, and_2_out, and_3_out, and_4_out, and_5_out, and_6_out, and_7_out, Beq, BGTZ, Bne,
       CLK, comparator_1_eq, comparator_2_gt, EN, ex_mem_1_p18, ex_mem_1_p19, ex_mem_1_p20, ex_mem_1_p21,
       ex_mem_1_p22, ex_mem_1_p23, Go, id_ex_1_alu_src_2, id_ex_1_beq_2, id_ex_1_bgtz_2, id_ex_1_bne_2,
       id_ex_1_jal_2, id_ex_1_jmp_2, id_ex_1_jr_2, id_ex_1_memtoreg_2, id_ex_1_memwrite_2,
       id_ex_1_regwrite_2, id_ex_1_sb_2, id_ex_1_shamt_2, id_ex_1_syscall_2, IR1, IR2, IR3, JAL, JMP, JR,
       MemToReg, MemWrite, mips_alu_1_equal, not_2_out, or_3_out, or_4_out, RegDst, register_2_q, RegWrite,
       RegWrite_num, RST, run, SB, Shamt, SignedExt, Syscall, W1, W2, W3;
  wire [1:0] ex_mem_1_p24, PCSrc;
  wire [3:0] adder_2_out_2, AluOP, decoder_1_out0, id_ex_1_alu_op_2, multiplexer_10_out;
  wire [4:0] ex_mem_1_p26, id_ex_1_w_num_2, mem_wb_1_w_num_2, multiplexer_2_out, multiplexer_3_out,
       multiplexer_4_out, multiplexer_5_out, multiplexer_8_out;
  wire [15:0] \LoadUse次数 , \总周期数 , \插入气泡数 , \无条件分支数 , \条件分支成功数 ;
  wire [27:0] adder_2_out;
  wire [31:0] adder_1_out, bit_extender_1_out, bit_extender_2_out, ex_mem_1_p17, ex_mem_1_p25, EX_PC,
       id_ex_1_o_imm, id_ex_1_o_ir, id_ex_1_o_r1, id_ex_1_o_r2, ID_PC, IF_PC, LedData, MEM_PC,
       mem_wb_1_memout_2, mips_alu_1_result, mips_ram_1_p8, mips_regifile_1_r1, mips_regifile_1_r2,
       multiplexer_1_out, multiplexer_6_out, multiplexer_7_out, multiplexer_9_out, multiplexer_11_out,
       multiplexer_12_out, rom_1_data, shifter_1_out, WB_PC;
  wire [31:2] ex_mem_1_p24_2;

  Button \u_总复位  (.out(RST));
  Button _1 (.out(IR1));
  Button _2 (.out(IR2));
  Button _3 (.out(IR3));
  Button \u_继续运行  (.out(Go));
  LED led_1 (.in(W1));
  LED led_2 (.in(W2));
  LED led_3 (.in(W3));
  not not_1 (EN, run);
  Multiplexer #(.select(2), .width(32), .enable("false")) multiplexer_1 (
    .in0({adder_2_out_2, adder_2_out}), .in1(adder_1_out), .in2({adder_2_out_2, out_1[25:0], 2'b00}),
    .in3(id_ex_1_o_r1), .out(multiplexer_1_out), .sel(PCSrc));
  Hex_Digit_Display hex_digit_display_1 (.value(LedData[31:28]));  // open: dp
  Register #(.width(32)) PC (.D(multiplexer_1_out), .en(run), .Q(IF_PC), .clk(CLK), .clr(RST));
  Hex_Digit_Display hex_digit_display_2 (.value(LedData[27:24]));  // open: dp
  Hex_Digit_Display hex_digit_display_3 (.value(LedData[23:20]));  // open: dp
  Adder #(.width(32)) adder_1 (
    .a(shifter_1_out), .b({adder_2_out_2, adder_2_out}), .out(adder_1_out));  // open: cin, cout
  Hex_Digit_Display hex_digit_display_4 (.value(LedData[19:16]));  // open: dp
  Hex_Digit_Display hex_digit_display_5 (.value(LedData[15:12]));  // open: dp
  Counter #(.width(16), .max('hffff)) counter_1 (
    .count(run), .Q(\总周期数 ), .clk(CLK), .clr(RST));  // open: load, D, carry
  Hex_Digit_Display hex_digit_display_6 (.value(LedData[11:8]));  // open: dp
  Hex_Digit_Display hex_digit_display_7 (.value(LedData[7:4]));  // open: dp
  Clock clock_1 (.out(CLK));
  ROM #(.addrWidth(24), .dataWidth(32)) rom_1 (.addr(IF_PC[25:2]), .data(rom_1_data));  // open: sel
  Adder #(.width(32)) adder_2 (.a(IF_PC), .b(32'h4), .out({adder_2_out_2, adder_2_out}));  // open: cin, cout
  Shifter #(.width(32)) shifter_1 (.in(id_ex_1_o_imm), .\dist (5'b00010), .out(shifter_1_out));
  Hex_Digit_Display hex_digit_display_8 (.value(LedData[3:0]));  // open: dp
  IF_ID if_id_1 (
    .I_PC(IF_PC), .I_IR(rom_1_data), .O_PC(ID_PC), .O_IR(out_1), .bubble(1'b0), .en(EN), .clk(CLK), .clr(RST));  // open: ExpAddr, ExpAddr_2, 预测跳转, 预测跳转_2
  // Probe on \总周期数 
  // Probe on \无条件分支数 
  // Probe on \条件分支成功数 
  // Probe on \插入气泡数 
  // Probe on \LoadUse次数 
  Multiplexer #(.width(5), .enable("false")) multiplexer_2 (
    .in0(out_1[20:16]), .in1(out_1[15:11]), .out(multiplexer_2_out), .sel(RegDst));
  assign bit_extender_1_out = {{16{out_1[15]}}, out_1[15:0]};  // Bit_Extender bit_extender_1
  assign bit_extender_2_out = {{16{1'b0}}, out_1[15:0]};  // Bit_Extender bit_extender_2
  // Probe on IF_PC[11:0]
  Multiplexer #(.width(5), .enable("false")) multiplexer_3 (
    .in0(out_1[25:21]), .in1(5'b00010), .out(multiplexer_3_out), .sel(Syscall));
  Multiplexer #(.width(5), .enable("false")) multiplexer_4 (
    .in0(out_1[20:16]), .in1(5'b00100), .out(multiplexer_4_out), .sel(Syscall));
  Multiplexer #(.width(5), .enable("false")) multiplexer_5 (
    .in0(multiplexer_2_out), .in1({5{1'b1}}), .out(multiplexer_5_out), .sel(JAL));
  // Probe on ID_PC[11:0]
  // Probe on MEM_PC[11:0]
  // Probe on EX_PC[11:0]
  MIPS_Regifile mips_regifile_1 (
    .Din(mem_wb_1_memout_2), .Clk(CLK), .R1(mips_regifile_1_r1), .R2(mips_regifile_1_r2), .WE(RegWrite_num),
    .W_num(mem_wb_1_w_num_2), .R1_num(multiplexer_3_out), .R2_num(multiplexer_4_out));
  Multiplexer #(.width(32), .enable("false")) multiplexer_6 (
    .in0(bit_extender_2_out), .in1(bit_extender_1_out), .out(multiplexer_6_out), .sel(SignedExt));
  // Probe on WB_PC[11:0]
  ID_EX id_ex_1 (
    .I_PC(ID_PC), .I_IR(out_1), .RegWrite(RegWrite), .MemtoReg(MemToReg), .MemWrite(MemWrite), .SB(SB),
    .ALU_SRC(AluSrcB), .BEQ(Beq), .BNE(Bne), .JR(JR), .JMP(JMP), .JAL(JAL), .BGTZ(BGTZ), .Shamt(Shamt),
    .ALU_OP(AluOP), .syscall(Syscall), .O_PC(EX_PC), .O_IR(id_ex_1_o_ir), .RegWrite_2(id_ex_1_regwrite_2),
    .MemtoReg_2(id_ex_1_memtoreg_2), .MemWrite_2(id_ex_1_memwrite_2), .SB_2(id_ex_1_sb_2),
    .ALU_SRC_2(id_ex_1_alu_src_2), .BEQ_2(id_ex_1_beq_2), .BNE_2(id_ex_1_bne_2), .JR_2(id_ex_1_jr_2),
    .JMP_2(id_ex_1_jmp_2), .JAL_2(id_ex_1_jal_2), .BGTZ_2(id_ex_1_bgtz_2), .Shamt_2(id_ex_1_shamt_2),
    .ALU_OP_2(id_ex_1_alu_op_2), .syscall_2(id_ex_1_syscall_2), .bubble(1'b0), .en(EN), .clk(CLK), .clr(RST),
    .I_R1(mips_regifile_1_r1), .I_R2(mips_regifile_1_r2), .O_R1(id_ex_1_o_r1), .O_R2(id_ex_1_o_r2),
    .I_Imm(multiplexer_6_out), .O_Imm(id_ex_1_o_imm), .W_num(multiplexer_5_out), .W_num_2(id_ex_1_w_num_2));  // open: sel, sel_2, ExpAddr, ExpAddr_2, 预测跳转, 预测跳转_2
  \硬布线控制器  \u_硬布线控制器_1  (
    .Func(out_1[5:0]), .OP(out_1[31:26]), .ALU_OP(AluOP), .MemToReg(MemToReg), .MemWrite(MemWrite),
    .ALU_SRC(AluSrcB), .RegWrite(RegWrite), .SysCALL(Syscall), .SignedExt(SignedExt), .RegDst(RegDst),
    .JR(JR), .JMP(JMP), .Beq(Beq), .Bne(Bne), .JAL(JAL), .SHAMT(Shamt), .SB(SB), .BGTZ(BGTZ));
  Multiplexer #(.width(32), .disabled(0), .enable("false")) multiplexer_7 (
    .in0(id_ex_1_o_r2), .in1(id_ex_1_o_imm), .out(multiplexer_7_out), .sel(id_ex_1_alu_src_2));
  and and_1 (and_1_out, ~comparator_1_eq, id_ex_1_syscall_2);  // AND_Gate
  and and_2 (and_2_out, comparator_1_eq, id_ex_1_syscall_2);
  Comparator #(.width(32)) comparator_1 (.a(32'h22), .b(id_ex_1_o_r1), .eq(comparator_1_eq));  // open: gt, lt
  Register #(.width(32)) register_1 (.D(id_ex_1_o_r2), .en(and_2_out), .Q(LedData), .clk(CLK), .clr(RST));
  Multiplexer #(.width(5), .enable("false")) multiplexer_8 (
    .in0(id_ex_1_o_r1[4:0]), .in1(out_1[10:6]), .out(multiplexer_8_out), .sel(id_ex_1_shamt_2));
  Comparator #(.width(32)) comparator_2 (.a(id_ex_1_o_r1), .b({32{1'b0}}), .gt(comparator_2_gt));  // open: eq, lt
  not not_2 (not_2_out, mips_alu_1_equal);
  MIPS_ALU mips_alu_1 (
    .X(id_ex_1_o_r1), .Y(multiplexer_7_out), .AluOP(id_ex_1_alu_op_2), .Equal(mips_alu_1_equal),
    .Result(mips_alu_1_result), .shamt(multiplexer_8_out));  // open: Result_2
  and and_3 (and_3_out, comparator_2_gt, id_ex_1_bgtz_2);
  and and_4 (and_4_out, not_2_out, id_ex_1_bne_2);
  and and_5 (and_5_out, mips_alu_1_equal, id_ex_1_beq_2);
  and and_6 (and_6_out, run, PCSrc[1]);
  Counter #(.width(16), .max('hffff)) counter_2 (
    .count(and_6_out), .Q(\无条件分支数 ), .clk(CLK), .clr(RST));  // open: load, D, carry
  or or_1 (PCSrc[1], id_ex_1_jal_2, id_ex_1_jmp_2, id_ex_1_jr_2);
  or or_2 (PCSrc[0], id_ex_1_jr_2, and_4_out, and_5_out, and_3_out);
  Counter #(.width(16), .max('hffff)) counter_3 (
    .count(and_7_out), .Q(\条件分支成功数 ), .clk(CLK), .clr(RST));  // open: load, D, carry
  and and_7 (and_7_out, run, or_3_out);
  or or_3 (or_3_out, and_4_out, and_5_out, and_3_out);
  // EX_MEM ex_mem_1: pin names not known; wires that end beside it: EX_PC, id_ex_1_o_ir, id_ex_1_regwrite_2, id_ex_1_memtoreg_2, id_ex_1_memwrite_2, id_ex_1_sb_2, id_ex_1_jal_2, and_1_out, mips_alu_1_result, id_ex_1_o_r2, id_ex_1_w_num_2, 1'b0, EN, CLK, RST, MEM_PC, ex_mem_1_p17, ex_mem_1_p18, ex_mem_1_p19, ex_mem_1_p20, ex_mem_1_p21, ex_mem_1_p22, ex_mem_1_p23, {ex_mem_1_p24_2, ex_mem_1_p24}, ex_mem_1_p25, ex_mem_1_p26
  not not_3 (run, register_2_q);
  Register #(.width(1)) register_2 (.D(1'b1), .en(ex_mem_1_p23), .Q(register_2_q), .clk(CLK), .clr(or_4_out));
  or or_4 (or_4_out, RST, Go);
  Decoder #(.select(2), .enable("false")) decoder_1 (
    .out0(decoder_1_out0[0]), .out1(decoder_1_out0[1]), .out2(decoder_1_out0[2]), .out3(decoder_1_out0[3]),
    .sel(ex_mem_1_p24));
  Multiplexer #(.width(32), .enable("false")) multiplexer_9 (
    .in0(ex_mem_1_p25), .in1({ex_mem_1_p25[7:0], ex_mem_1_p25[7:0], ex_mem_1_p25[7:0], ex_mem_1_p25[7:0]}),
    .out(multiplexer_9_out), .sel(ex_mem_1_p21));
  Multiplexer #(.width(4), .enable("false")) multiplexer_10 (
    .in0(4'b1111), .in1(decoder_1_out0), .out(multiplexer_10_out), .sel(ex_mem_1_p21));
  // MIPS_RAM mips_ram_1: pin names not known; wires that end beside it: ex_mem_1_p24_2[25:2], multiplexer_9_out, ex_mem_1_p20, multiplexer_10_out, CLK, 1'b1, RST, mips_ram_1_p8
  Multiplexer #(.width(32), .enable("false")) multiplexer_11 (
    .in0({ex_mem_1_p24_2, ex_mem_1_p24}), .in1(mips_ram_1_p8), .out(multiplexer_11_out), .sel(ex_mem_1_p19));
  Multiplexer #(.width(32), .enable("false")) multiplexer_12 (
    .in0(multiplexer_11_out), .in1({adder_2_out_2, adder_2_out}), .out(multiplexer_12_out), .sel(ex_mem_1_p22));
  MEM_WB mem_wb_1 (
    .I_PC(MEM_PC), .I_IR(ex_mem_1_p17), .RegWrite(ex_mem_1_p18), .W_num(ex_mem_1_p26), .O_PC(WB_PC),
    .RegWrite_2(RegWrite_num), .W_num_2(mem_wb_1_w_num_2), .bubble(1'b0), .en(EN), .clk(CLK), .clr(RST),
    .MemOut(multiplexer_12_out), .MemOut_2(mem_wb_1_memout_2));  // open: O_IR, res1, res1_2, MemtoReg, MemtoReg_2, jal, jal_2

  // Other names for the same wires on the sheet: Func[5:0] = out_1[5:0]; Op[5:0] = out_1[31:26]; PC[31:0] = IF_PC

  // Notes on the sheet:
  //   中断源
  //   中断等待指示
  //   数码管输出
  //   syscall: if $v0(2) == 34 then print $a0(4) else pause
  //   指令存储器
  //   指令字
  //   contents of rom_1 (hex, n*v repeats v):
  //   20100000 20110000 20120000 20130000 36100000 36310001 36520002 36730003 ae100000 ae110004 ae120008
  //   ae13000c 2002000a 20110000 20120000 20130000 c
  //   OP
  //   Func
  //   rs
  //   rt
  //   rd
  //   流水调试日志用
endmodule

// 源寄存器使用情况
module \源寄存器使用情况  (
  input  OP0,
  input  OP1,
  input  OP2,
  input  OP3,
  input  OP4,
  input  OP5,
  input  F0,
  input  F1,
  input  F2,
  input  F3,
  input  F4,
  input  F5,
  output R1_Used,
  output R2_Used
);

  wire and_1_out, and_2_out, and_3_out, and_4_out, and_5_out, and_6_out, and_7_out, and_8_out, and_9_out,
       and_10_out, and_11_out, and_12_out, and_13_out, and_14_out, and_15_out, and_16_out, and_17_out,
       and_18_out, and_19_out, and_20_out, and_21_out, and_22_out, and_23_out, and_24_out, and_25_out,
       and_26_out, and_27_out, and_28_out, and_29_out, and_30_out, and_31_out, and_32_out, and_33_out,
       and_34_out, and_35_out, and_36_out, and_37_out, and_38_out, and_39_out, and_40_out, and_41_out,
       and_42_out, and_43_out, not_1_out, not_2_out, not_3_out, not_4_out, not_5_out, not_6_out, not_7_out,
       not_8_out, not_9_out, not_10_out, not_11_out, not_12_out, not_13_out, not_14_out, not_15_out,
       not_16_out, not_17_out, not_18_out, not_19_out, not_20_out, not_21_out, not_22_out, not_23_out,
       not_24_out, not_25_out, not_26_out, not_27_out, not_28_out, not_29_out, not_30_out, not_31_out,
       not_32_out, not_33_out, not_34_out, not_35_out, not_36_out, not_37_out, not_38_out, not_39_out,
       not_40_out, not_41_out, not_42_out, not_43_out, not_44_out, not_45_out, not_46_out, not_47_out,
       not_48_out, not_49_out, not_50_out, not_51_out, not_52_out, not_53_out, not_54_out, not_55_out,
       not_56_out, not_57_out, not_58_out, not_59_out, not_60_out, not_61_out, not_62_out, not_63_out,
       not_64_out, not_65_out, not_66_out, not_67_out, not_68_out, not_69_out, not_70_out, not_71_out,
       not_72_out, not_73_out, not_74_out, not_75_out, not_76_out, not_77_out, not_78_out, not_79_out,
       not_80_out, not_81_out, not_82_out, not_83_out, not_84_out, not_85_out, not_86_out, not_87_out,
       not_88_out, not_89_out, not_90_out, not_91_out, not_92_out, not_93_out, not_94_out, not_95_out,
       not_96_out, not_97_out, not_98_out, not_99_out, not_100_out, not_101_out, not_102_out, not_103_out,
       not_104_out, not_105_out, not_106_out, not_107_out, not_108_out, not_109_out, not_110_out,
       not_111_out, not_112_out, not_113_out, not_114_out, not_115_out, not_116_out, not_117_out,
       not_118_out, not_119_out, not_120_out, not_121_out, not_122_out, not_123_out, not_124_out,
       not_125_out, not_126_out, not_127_out, not_128_out, not_129_out, not_130_out, not_131_out,
       not_132_out, not_133_out, not_134_out, not_135_out, not_136_out, not_137_out, not_138_out,
       not_139_out, not_140_out, not_141_out, not_142_out, not_143_out, not_144_out, not_145_out,
       not_146_out, not_147_out, not_148_out, not_149_out, not_150_out, not_151_out, not_152_out,
       not_153_out, not_154_out, not_155_out, not_156_out, not_157_out, not_158_out, not_159_out,
       not_160_out, not_161_out, not_162_out, not_163_out, not_164_out, not_165_out, not_166_out,
       not_167_out, not_168_out, not_169_out, not_170_out, not_171_out, not_172_out, not_173_out,
       not_174_out, not_175_out, not_176_out, not_177_out, not_178_out, not_179_out, not_180_out,
       not_181_out, not_182_out, not_183_out, not_184_out, not_185_out, not_186_out, not_187_out,
       not_188_out, not_189_out, not_190_out, not_191_out, not_192_out, not_193_out, not_194_out,
       not_195_out, not_196_out, not_197_out, not_198_out, not_199_out, not_200_out, not_201_out,
       not_202_out, not_203_out, not_204_out, not_205_out, not_206_out, not_207_out, not_208_out,
       not_209_out, not_210_out, not_211_out, not_212_out, not_213_out, not_214_out, not_215_out,
       not_216_out, not_217_out, not_218_out, not_219_out, not_220_out, not_221_out, not_222_out,
       not_223_out, not_224_out, not_225_out, not_226_out, not_227_out, not_228_out, not_229_out,
       not_230_out, not_231_out, not_232_out, not_233_out, not_234_out, not_235_out, not_236_out,
       not_237_out, not_238_out, not_239_out, not_240_out, not_241_out, not_242_out, not_243_out,
       not_244_out, not_245_out, not_246_out, not_247_out, not_248_out, not_249_out, not_250_out,
       not_251_out, not_252_out, not_253_out, not_254_out, not_255_out, not_256_out, not_257_out,
       not_258_out, not_259_out, not_260_out, not_261_out, not_262_out, not_263_out, not_264_out,
       not_265_out, not_266_out, not_267_out, not_268_out, not_269_out, not_270_out, not_271_out,
       not_272_out, not_273_out, not_274_out, not_275_out, not_276_out, not_277_out, not_278_out,
       not_279_out, not_280_out, not_281_out, not_282_out, not_283_out, not_284_out, not_285_out,
       not_286_out, not_287_out, not_288_out, not_289_out, not_290_out, not_291_out, not_292_out,
       not_293_out, not_294_out, not_295_out, not_296_out, not_297_out, not_298_out, not_299_out,
       not_300_out, not_301_out, not_302_out, not_303_out, not_304_out, not_305_out, not_306_out,
       not_307_out, not_308_out, not_309_out, not_310_out, not_311_out, not_312_out, not_313_out,
       not_314_out, not_315_out, not_316_out, not_317_out;

  not not_1 (not_1_out, OP5);
  not not_2 (not_2_out, OP4);
  not not_3 (not_3_out, OP3);
  not not_4 (not_4_out, OP2);
  not not_5 (not_5_out, OP1);
  not not_6 (not_6_out, OP0);
  not not_7 (not_7_out, F4);
  not not_8 (not_8_out, F3);
  not not_9 (not_9_out, F2);
  not not_10 (not_10_out, F1);
  not not_11 (not_11_out, F0);
  not not_12 (not_12_out, OP5);
  not not_13 (not_13_out, OP4);
  not not_14 (not_14_out, OP3);
  not not_15 (not_15_out, OP2);
  not not_16 (not_16_out, OP1);
  not not_17 (not_17_out, OP0);
  not not_18 (not_18_out, F4);
  not not_19 (not_19_out, F3);
  not not_20 (not_20_out, F2);
  not not_21 (not_21_out, F1);
  not not_22 (not_22_out, OP5);
  not not_23 (not_23_out, OP4);
  not not_24 (not_24_out, OP3);
  not not_25 (not_25_out, OP2);
  not not_26 (not_26_out, OP1);
  not not_27 (not_27_out, OP0);
  not not_28 (not_28_out, F4);
  not not_29 (not_29_out, F3);
  not not_30 (not_30_out, F2);
  not not_31 (not_31_out, F0);
  not not_32 (not_32_out, OP5);
  not not_33 (not_33_out, OP4);
  not not_34 (not_34_out, OP3);
  not not_35 (not_35_out, OP2);
  not not_36 (not_36_out, OP1);
  not not_37 (not_37_out, OP0);
  not not_38 (not_38_out, F4);
  not not_39 (not_39_out, F3);
  not not_40 (not_40_out, F1);
  not not_41 (not_41_out, F0);
  not not_42 (not_42_out, OP5);
  not not_43 (not_43_out, OP4);
  not not_44 (not_44_out, OP3);
  not not_45 (not_45_out, OP2);
  not not_46 (not_46_out, OP1);
  not not_47 (not_47_out, OP0);
  not not_48 (not_48_out, F4);
  not not_49 (not_49_out, F3);
  not not_50 (not_50_out, F1);
  not not_51 (not_51_out, OP5);
  not not_52 (not_52_out, OP4);
  not not_53 (not_53_out, OP3);
  not not_54 (not_54_out, OP2);
  not not_55 (not_55_out, OP1);
  not not_56 (not_56_out, OP0);
  not not_57 (not_57_out, F4);
  not not_58 (not_58_out, F3);
  not not_59 (not_59_out, OP5);
  not not_60 (not_60_out, OP4);
  not not_61 (not_61_out, OP3);
  not not_62 (not_62_out, OP2);
  not not_63 (not_63_out, OP1);
  not not_64 (not_64_out, OP0);
  not not_65 (not_65_out, F4);
  not not_66 (not_66_out, F2);
  not not_67 (not_67_out, F0);
  not not_68 (not_68_out, OP5);
  not not_69 (not_69_out, OP4);
  not not_70 (not_70_out, OP3);
  not not_71 (not_71_out, OP2);
  not not_72 (not_72_out, OP1);
  not not_73 (not_73_out, OP0);
  not not_74 (not_74_out, F4);
  not not_75 (not_75_out, F2);
  not not_76 (not_76_out, OP5);
  not not_77 (not_77_out, OP4);
  not not_78 (not_78_out, OP3);
  not not_79 (not_79_out, OP2);
  not not_80 (not_80_out, OP1);
  not not_81 (not_81_out, OP0);
  not not_82 (not_82_out, F5);
  not not_83 (not_83_out, F4);
  not not_84 (not_84_out, F2);
  not not_85 (not_85_out, F1);
  not not_86 (not_86_out, F0);
  not not_87 (not_87_out, OP5);
  not not_88 (not_88_out, OP4);
  not not_89 (not_89_out, OP3);
  not not_90 (not_90_out, OP2);
  not not_91 (not_91_out, OP1);
  not not_92 (not_92_out, OP0);
  not not_93 (not_93_out, F5);
  not not_94 (not_94_out, F4);
  not not_95 (not_95_out, F1);
  not not_96 (not_96_out, F0);
  not not_97 (not_97_out, OP5);
  not not_98 (not_98_out, OP4);
  not not_99 (not_99_out, OP3);
  not not_100 (not_100_out, OP2);
  not not_101 (not_101_out, OP0);
  not not_102 (not_102_out, OP5);
  not not_103 (not_103_out, OP4);
  not not_104 (not_104_out, OP3);
  not not_105 (not_105_out, OP2);
  not not_106 (not_106_out, OP5);
  not not_107 (not_107_out, OP4);
  not not_108 (not_108_out, OP3);
  not not_109 (not_109_out, OP1);
  not not_110 (not_110_out, OP0);
  not not_111 (not_111_out, OP5);
  not not_112 (not_112_out, OP4);
  not not_113 (not_113_out, OP3);
  not not_114 (not_114_out, OP1);
  not not_115 (not_115_out, OP5);
  not not_116 (not_116_out, OP4);
  not not_117 (not_117_out, OP2);
  not not_118 (not_118_out, OP1);
  not not_119 (not_119_out, OP0);
  not not_120 (not_120_out, OP5);
  not not_121 (not_121_out, OP4);
  not not_122 (not_122_out, OP1);
  not not_123 (not_123_out, OP0);
  not not_124 (not_124_out, OP5);
  not not_125 (not_125_out, OP4);
  not not_126 (not_126_out, OP2);
  not not_127 (not_127_out, OP1);
  not not_128 (not_128_out, OP5);
  not not_129 (not_129_out, OP4);
  not not_130 (not_130_out, OP2);
  not not_131 (not_131_out, OP0);
  not not_132 (not_132_out, OP5);
  not not_133 (not_133_out, OP4);
  not not_134 (not_134_out, OP1);
  not not_135 (not_135_out, OP4);
  not not_136 (not_136_out, OP3);
  not not_137 (not_137_out, OP2);
  not not_138 (not_138_out, OP4);
  not not_139 (not_139_out, OP2);
  not not_140 (not_140_out, OP5);
  not not_141 (not_141_out, OP4);
  not not_142 (not_142_out, OP3);
  not not_143 (not_143_out, OP2);
  not not_144 (not_144_out, OP1);
  not not_145 (not_145_out, OP0);
  not not_146 (not_146_out, F5);
  not not_147 (not_147_out, F4);
  not not_148 (not_148_out, F3);
  not not_149 (not_149_out, F0);
  not not_150 (not_150_out, OP5);
  not not_151 (not_151_out, OP4);
  not not_152 (not_152_out, OP3);
  not not_153 (not_153_out, OP2);
  not not_154 (not_154_out, OP1);
  not not_155 (not_155_out, OP0);
  not not_156 (not_156_out, F4);
  not not_157 (not_157_out, F3);
  not not_158 (not_158_out, F2);
  not not_159 (not_159_out, OP4);
  not not_160 (not_160_out, OP2);
  not not_161 (not_161_out, OP1);
  not not_162 (not_162_out, OP0);
  not not_163 (not_163_out, OP5);
  not not_164 (not_164_out, OP4);
  not not_165 (not_165_out, OP3);
  not not_166 (not_166_out, OP5);
  not not_167 (not_167_out, OP4);
  not not_168 (not_168_out, OP3);
  not not_169 (not_169_out, OP2);
  not not_170 (not_170_out, OP1);
  not not_171 (not_171_out, OP0);
  not not_172 (not_172_out, F5);
  not not_173 (not_173_out, F4);
  not not_174 (not_174_out, F3);
  not not_175 (not_175_out, F2);
  not not_176 (not_176_out, F1);
  not not_177 (not_177_out, F0);
  not not_178 (not_178_out, OP5);
  not not_179 (not_179_out, OP4);
  not not_180 (not_180_out, OP3);
  not not_181 (not_181_out, OP2);
  not not_182 (not_182_out, OP1);
  not not_183 (not_183_out, OP0);
  not not_184 (not_184_out, F5);
  not not_185 (not_185_out, F4);
  not not_186 (not_186_out, F3);
  not not_187 (not_187_out, F2);
  not not_188 (not_188_out, OP5);
  not not_189 (not_189_out, OP4);
  not not_190 (not_190_out, OP3);
  not not_191 (not_191_out, OP2);
  not not_192 (not_192_out, OP1);
  not not_193 (not_193_out, OP0);
  not not_194 (not_194_out, F5);
  not not_195 (not_195_out, F4);
  not not_196 (not_196_out, F3);
  not not_197 (not_197_out, F2);
  not not_198 (not_198_out, F0);
  not not_199 (not_199_out, OP5);
  not not_200 (not_200_out, OP4);
  not not_201 (not_201_out, OP3);
  not not_202 (not_202_out, OP2);
  not not_203 (not_203_out, OP1);
  not not_204 (not_204_out, OP0);
  not not_205 (not_205_out, F4);
  not not_206 (not_206_out, F3);
  not not_207 (not_207_out, F2);
  not not_208 (not_208_out, F1);
  not not_209 (not_209_out, F0);
  not not_210 (not_210_out, OP5);
  not not_211 (not_211_out, OP4);
  not not_212 (not_212_out, OP3);
  not not_213 (not_213_out, OP2);
  not not_214 (not_214_out, OP1);
  not not_215 (not_215_out, OP0);
  not not_216 (not_216_out, F4);
  not not_217 (not_217_out, F3);
  not not_218 (not_218_out, F2);
  not not_219 (not_219_out, F1);
  not not_220 (not_220_out, OP5);
  not not_221 (not_221_out, OP4);
  not not_222 (not_222_out, OP3);
  not not_223 (not_223_out, OP2);
  not not_224 (not_224_out, OP1);
  not not_225 (not_225_out, OP0);
  not not_226 (not_226_out, F4);
  not not_227 (not_227_out, F3);
  not not_228 (not_228_out, F2);
  not not_229 (not_229_out, F0);
  not not_230 (not_230_out, OP5);
  not not_231 (not_231_out, OP4);
  not not_232 (not_232_out, OP3);
  not not_233 (not_233_out, OP2);
  not not_234 (not_234_out, OP1);
  not not_235 (not_235_out, OP0);
  not not_236 (not_236_out, F4);
  not not_237 (not_237_out, F3);
  not not_238 (not_238_out, F1);
  not not_239 (not_239_out, F0);
  not not_240 (not_240_out, OP5);
  not not_241 (not_241_out, OP4);
  not not_242 (not_242_out, OP3);
  not not_243 (not_243_out, OP2);
  not not_244 (not_244_out, OP1);
  not not_245 (not_245_out, OP0);
  not not_246 (not_246_out, F4);
  not not_247 (not_247_out, F3);
  not not_248 (not_248_out, F1);
  not not_249 (not_249_out, OP5);
  not not_250 (not_250_out, OP4);
  not not_251 (not_251_out, OP3);
  not not_252 (not_252_out, OP2);
  not not_253 (not_253_out, OP1);
  not not_254 (not_254_out, OP0);
  not not_255 (not_255_out, F4);
  not not_256 (not_256_out, F3);
  not not_257 (not_257_out, OP5);
  not not_258 (not_258_out, OP4);
  not not_259 (not_259_out, OP3);
  not not_260 (not_260_out, OP2);
  not not_261 (not_261_out, OP1);
  not not_262 (not_262_out, OP0);
  not not_263 (not_263_out, F4);
  not not_264 (not_264_out, F2);
  not not_265 (not_265_out, F0);
  not not_266 (not_266_out, OP5);
  not not_267 (not_267_out, OP4);
  not not_268 (not_268_out, OP3);
  not not_269 (not_269_out, OP2);
  not not_270 (not_270_out, OP1);
  not not_271 (not_271_out, OP0);
  not not_272 (not_272_out, F4);
  not not_273 (not_273_out, F2);
  not not_274 (not_274_out, OP5);
  not not_275 (not_275_out, OP4);
  not not_276 (not_276_out, OP3);
  not not_277 (not_277_out, OP2);
  not not_278 (not_278_out, OP1);
  not not_279 (not_279_out, OP0);
  not not_280 (not_280_out, F5);
  not not_281 (not_281_out, F4);
  not not_282 (not_282_out, F1);
  not not_283 (not_283_out, F0);
  not not_284 (not_284_out, OP5);
  not not_285 (not_285_out, OP4);
  not not_286 (not_286_out, OP3);
  not not_287 (not_287_out, OP1);
  not not_288 (not_288_out, OP0);
  not not_289 (not_289_out, OP5);
  not not_290 (not_290_out, OP4);
  not not_291 (not_291_out, OP3);
  not not_292 (not_292_out, OP1);
  not not_293 (not_293_out, OP4);
  not not_294 (not_294_out, OP2);
  not not_295 (not_295_out, OP5);
  not not_296 (not_296_out, OP4);
  not not_297 (not_297_out, OP3);
  not not_298 (not_298_out, OP2);
  not not_299 (not_299_out, OP1);
  not not_300 (not_300_out, OP0);
  not not_301 (not_301_out, F5);
  not not_302 (not_302_out, F4);
  not not_303 (not_303_out, F3);
  not not_304 (not_304_out, F0);
  not not_305 (not_305_out, OP5);
  not not_306 (not_306_out, OP4);
  not not_307 (not_307_out, OP3);
  not not_308 (not_308_out, OP2);
  not not_309 (not_309_out, OP1);
  not not_310 (not_310_out, OP0);
  not not_311 (not_311_out, F4);
  not not_312 (not_312_out, F3);
  not not_313 (not_313_out, F2);
  not not_314 (not_314_out, OP4);
  not not_315 (not_315_out, OP2);
  not not_316 (not_316_out, OP1);
  not not_317 (not_317_out, OP0);
  and and_1 (and_1_out, not_1_out, not_2_out, not_3_out, not_4_out, not_5_out, not_6_out, F5, not_7_out, not_8_out, not_9_out, not_10_out, not_11_out);
  and and_2 (and_2_out, not_12_out, not_13_out, not_14_out, not_15_out, not_16_out, not_17_out, F5, not_18_out, not_19_out, not_20_out, not_21_out, F0);
  and and_3 (and_3_out, not_22_out, not_23_out, not_24_out, not_25_out, not_26_out, not_27_out, F5, not_28_out, not_29_out, not_30_out, F1, not_31_out);
  and and_4 (and_4_out, not_32_out, not_33_out, not_34_out, not_35_out, not_36_out, not_37_out, F5, not_38_out, not_39_out, F2, not_40_out, not_41_out);
  and and_5 (and_5_out, not_42_out, not_43_out, not_44_out, not_45_out, not_46_out, not_47_out, F5, not_48_out, not_49_out, F2, not_50_out, F0);
  and and_6 (and_6_out, not_51_out, not_52_out, not_53_out, not_54_out, not_55_out, not_56_out, F5, not_57_out, not_58_out, F2, F1, F0);
  and and_7 (and_7_out, not_59_out, not_60_out, not_61_out, not_62_out, not_63_out, not_64_out, F5, not_65_out, F3, not_66_out, F1, not_67_out);
  and and_8 (and_8_out, not_68_out, not_69_out, not_70_out, not_71_out, not_72_out, not_73_out, F5, not_74_out, F3, not_75_out, F1, F0);
  and and_9 (and_9_out, not_76_out, not_77_out, not_78_out, not_79_out, not_80_out, not_81_out, not_82_out, not_83_out, F3, not_84_out, not_85_out, not_86_out);
  and and_10 (and_10_out, not_87_out, not_88_out, not_89_out, not_90_out, not_91_out, not_92_out, not_93_out, not_94_out, F3, F2, not_95_out, not_96_out);
  and and_11 (and_11_out, not_97_out, not_98_out, not_99_out, not_100_out, OP1, not_101_out);
  and and_12 (and_12_out, not_102_out, not_103_out, not_104_out, not_105_out, OP1, OP0);
  and and_13 (and_13_out, not_106_out, not_107_out, not_108_out, OP2, not_109_out, not_110_out);
  and and_14 (and_14_out, not_111_out, not_112_out, not_113_out, OP2, not_114_out, OP0);
  and and_15 (and_15_out, not_115_out, not_116_out, OP3, not_117_out, not_118_out, not_119_out);
  and and_16 (and_16_out, not_120_out, not_121_out, OP3, OP2, not_122_out, not_123_out);
  and and_17 (and_17_out, not_124_out, not_125_out, OP3, not_126_out, not_127_out, OP0);
  and and_18 (and_18_out, not_128_out, not_129_out, OP3, not_130_out, OP1, not_131_out);
  and and_19 (and_19_out, not_132_out, not_133_out, OP3, OP2, not_134_out, OP0);
  and and_20 (and_20_out, OP5, not_135_out, not_136_out, not_137_out, OP1, OP0);
  and and_21 (and_21_out, OP5, not_138_out, OP3, not_139_out, OP1, OP0);
  and and_22 (and_22_out, not_140_out, not_141_out, not_142_out, not_143_out, not_144_out, not_145_out, not_146_out, not_147_out, not_148_out, F2, F1, not_149_out);
  and and_23 (and_23_out, not_150_out, not_151_out, not_152_out, not_153_out, not_154_out, not_155_out, F5, not_156_out, not_157_out, not_158_out, F1, F0);
  and and_24 (and_24_out, OP5, not_159_out, OP3, not_160_out, not_161_out, not_162_out);
  and and_25 (and_25_out, not_163_out, not_164_out, not_165_out, OP2, OP1, OP0);
  and and_26 (and_26_out, not_166_out, not_167_out, not_168_out, not_169_out, not_170_out, not_171_out, not_172_out, not_173_out, not_174_out, not_175_out, not_176_out, not_177_out);
  and and_27 (and_27_out, not_178_out, not_179_out, not_180_out, not_181_out, not_182_out, not_183_out, not_184_out, not_185_out, not_186_out, not_187_out, F1, F0);
  and and_28 (and_28_out, not_188_out, not_189_out, not_190_out, not_191_out, not_192_out, not_193_out, not_194_out, not_195_out, not_196_out, not_197_out, F1, not_198_out);
  and and_29 (and_29_out, not_199_out, not_200_out, not_201_out, not_202_out, not_203_out, not_204_out, F5, not_205_out, not_206_out, not_207_out, not_208_out, not_209_out);
  and and_30 (and_30_out, not_210_out, not_211_out, not_212_out, not_213_out, not_214_out, not_215_out, F5, not_216_out, not_217_out, not_218_out, not_219_out, F0);
  and and_31 (and_31_out, not_220_out, not_221_out, not_222_out, not_223_out, not_224_out, not_225_out, F5, not_226_out, not_227_out, not_228_out, F1, not_229_out);
  and and_32 (and_32_out, not_230_out, not_231_out, not_232_out, not_233_out, not_234_out, not_235_out, F5, not_236_out, not_237_out, F2, not_238_out, not_239_out);
  and and_33 (and_33_out, not_240_out, not_241_out, not_242_out, not_243_out, not_244_out, not_245_out, F5, not_246_out, not_247_out, F2, not_248_out, F0);
  and and_34 (and_34_out, not_249_out, not_250_out, not_251_out, not_252_out, not_253_out, not_254_out, F5, not_255_out, not_256_out, F2, F1, F0);
  and and_35 (and_35_out, not_257_out, not_258_out, not_259_out, not_260_out, not_261_out, not_262_out, F5, not_263_out, F3, not_264_out, F1, not_265_out);
  and and_36 (and_36_out, not_266_out, not_267_out, not_268_out, not_269_out, not_270_out, not_271_out, F5, not_272_out, F3, not_273_out, F1, F0);
  and and_37 (and_37_out, not_274_out, not_275_out, not_276_out, not_277_out, not_278_out, not_279_out, not_280_out, not_281_out, F3, F2, not_282_out, not_283_out);
  and and_38 (and_38_out, not_284_out, not_285_out, not_286_out, OP2, not_287_out, not_288_out);
  and and_39 (and_39_out, not_289_out, not_290_out, not_291_out, OP2, not_292_out, OP0);
  and and_40 (and_40_out, OP5, not_293_out, OP3, not_294_out, OP1, OP0);
  and and_41 (and_41_out, not_295_out, not_296_out, not_297_out, not_298_out, not_299_out, not_300_out, not_301_out, not_302_out, not_303_out, F2, F1, not_304_out);
  and and_42 (and_42_out, not_305_out, not_306_out, not_307_out, not_308_out, not_309_out, not_310_out, F5, not_311_out, not_312_out, not_313_out, F1, F0);
  and and_43 (and_43_out, OP5, not_314_out, OP3, not_315_out, not_316_out, not_317_out);
  or or_1 (R1_Used, and_1_out, and_2_out, and_3_out, and_4_out, and_5_out, and_6_out, and_7_out, and_8_out, and_9_out, and_10_out, and_11_out, and_12_out, and_13_out, and_14_out, and_15_out, and_16_out, and_17_out, and_18_out, and_19_out, and_20_out, and_21_out, and_22_out, and_23_out, and_24_out, and_25_out);
  or or_2 (R2_Used, and_26_out, and_27_out, and_28_out, and_29_out, and_30_out, and_31_out, and_32_out, and_33_out, and_34_out, and_35_out, and_36_out, and_37_out, and_38_out, and_39_out, and_40_out, and_41_out, and_42_out, and_43_out);
endmodule

module \数据相关检测  (
  input  [5:0] OP,
  input  [4:0] EX_WriteReg_num,
  input  EX_RegWrite,
  input  [4:0] MEM_WriteReg_num,
  input  MEM_RegWrite,
  input  [5:0] Func,
  input  [4:0] ID_R1_num,
  input  [4:0] ID_R2_num,
  output \数据相关 
);

  wire and_1_out, and_2_out, and_3_out, and_4_out, and_5_out, and_6_out, comparator_1_eq, comparator_2_eq,
       comparator_3_eq, comparator_4_eq, comparator_5_eq, comparator_6_eq, or_1_out, or_2_out, R1_Used,
       R2_Used;

  \源寄存器使用情况  \u_源寄存器使用情况_1  (
    .OP0(OP[0]), .OP1(OP[1]), .OP2(OP[2]), .OP3(OP[3]), .OP4(OP[4]), .OP5(OP[5]), .F0(Func[0]), .F1(Func[1]),
    .F2(Func[2]), .F3(Func[3]), .F4(Func[4]), .F5(Func[5]), .R1_Used(R1_Used), .R2_Used(R2_Used));
  Comparator #(.width(5)) comparator_1 (.a(ID_R1_num), .b(EX_WriteReg_num), .eq(comparator_1_eq));  // open: gt, lt
  Comparator #(.width(5)) comparator_2 (.a(ID_R1_num), .b(MEM_WriteReg_num), .eq(comparator_2_eq));  // open: gt, lt
  Comparator #(.width(5)) comparator_3 (.a(ID_R2_num), .b(EX_WriteReg_num), .eq(comparator_3_eq));  // open: gt, lt
  Comparator #(.width(5)) comparator_4 (.a(ID_R2_num), .b(MEM_WriteReg_num), .eq(comparator_4_eq));  // open: gt, lt
  and and_1 (and_1_out, R1_Used, comparator_1_eq, EX_RegWrite);
  and and_2 (and_2_out, R1_Used, comparator_2_eq, MEM_RegWrite);
  and and_3 (and_3_out, R2_Used, comparator_3_eq, EX_RegWrite);
  and and_4 (and_4_out, R2_Used, comparator_4_eq, MEM_RegWrite);
  Comparator #(.width(5)) comparator_5 (.a({5{1'b0}}), .b(ID_R1_num), .eq(comparator_5_eq));  // open: gt, lt
  or or_1 (or_1_out, and_1_out, and_2_out);
  Comparator #(.width(5)) comparator_6 (.a({5{1'b0}}), .b(ID_R2_num), .eq(comparator_6_eq));  // open: gt, lt
  or or_2 (or_2_out, and_3_out, and_4_out);
  and and_5 (and_5_out, ~comparator_5_eq, or_1_out);  // AND_Gate
  and and_6 (and_6_out, ~comparator_6_eq, or_2_out);  // AND_Gate
  or or_3 (\数据相关 , and_5_out, and_6_out);

  // Other names for the same wires on the sheet: OP_CODE[5:0] = OP
endmodule

// IF/ID
module IF_ID (
  input  bubble,
  input  en,
  input  clk,
  input  clr,
  input  [31:0] I_PC,
  input  [31:0] I_IR,
  input  [31:0] ExpAddr,
  input  \预测跳转 ,
  output [31:0] O_PC,
  output [31:0] O_IR,
  output [31:0] ExpAddr_2,
  output \预测跳转_2 
);

  wire multiplexer_4_out, not_1_out;
  wire [31:0] multiplexer_1_out, multiplexer_2_out, multiplexer_3_out;

  not not_1 (not_1_out, en);
  Multiplexer #(.width(32), .enable("false")) multiplexer_1 (
    .in0(I_PC), .in1({32{1'b0}}), .out(multiplexer_1_out), .sel(bubble));
  Multiplexer #(.width(32), .enable("false")) multiplexer_2 (
    .in0(I_IR), .in1({32{1'b0}}), .out(multiplexer_2_out), .sel(bubble));
  Multiplexer #(.width(32), .enable("false")) multiplexer_3 (
    .in0(ExpAddr), .in1({32{1'b0}}), .out(multiplexer_3_out), .sel(bubble));
  Multiplexer #(.enable("false")) multiplexer_4 (.in0(\预测跳转 ), .in1(1'b0), .out(multiplexer_4_out), .sel(bubble));
  Register #(.width(32)) register_1 (.D(multiplexer_1_out), .en(not_1_out), .Q(O_PC), .clk(clk), .clr(clr));
  Register #(.width(32)) register_2 (.D(multiplexer_2_out), .en(not_1_out), .Q(O_IR), .clk(clk), .clr(clr));
  Register #(.width(32)) register_3 (.D(multiplexer_3_out), .en(not_1_out), .Q(ExpAddr_2), .clk(clk), .clr(clr));
  Register #(.width(1)) register_4 (.D(multiplexer_4_out), .en(not_1_out), .Q(\预测跳转_2 ), .clk(clk), .clr(clr));
endmodule

// ID/EX
module ID_EX (
  input  bubble,
  input  en,
  input  clk,
  input  clr,
  input  [31:0] I_PC,
  input  [31:0] I_IR,
  input  RegWrite,
  input  MemtoReg,
  input  MemWrite,
  input  SB,
  input  ALU_SRC,
  input  BEQ,
  input  BNE,
  input  JR,
  input  JMP,
  input  JAL,
  input  BGTZ,
  input  Shamt,
  input  [3:0] ALU_OP,
  input  syscall,
  input  [4:0] W_num,
  input  [31:0] I_R1,
  input  [31:0] I_R2,
  input  [31:0] I_Imm,
  input  [3:0] sel,
  input  [31:0] ExpAddr,
  input  \预测跳转 ,
  output [31:0] O_PC,
  output [31:0] O_IR,
  output RegWrite_2,
  output MemtoReg_2,
  output MemWrite_2,
  output SB_2,
  output ALU_SRC_2,
  output BEQ_2,
  output BNE_2,
  output JR_2,
  output JMP_2,
  output JAL_2,
  output BGTZ_2,
  output Shamt_2,
  output [3:0] ALU_OP_2,
  output syscall_2,
  output [4:0] W_num_2,
  output [31:0] O_R1,
  output [31:0] O_R2,
  output [31:0] O_Imm,
  output [3:0] sel_2,
  output [31:0] ExpAddr_2,
  output \预测跳转_2 
);

  wire multiplexer_3_out, multiplexer_4_out, multiplexer_5_out, multiplexer_6_out, multiplexer_7_out,
       multiplexer_8_out, multiplexer_9_out, multiplexer_10_out, multiplexer_11_out, multiplexer_12_out,
       multiplexer_13_out, multiplexer_14_out, multiplexer_16_out, multiplexer_23_out, not_1_out;
  wire [3:0] multiplexer_15_out, multiplexer_21_out;
  wire [4:0] multiplexer_17_out;
  wire [31:0] multiplexer_1_out, multiplexer_2_out, multiplexer_18_out, multiplexer_19_out,
       multiplexer_20_out, multiplexer_22_out;

  not not_1 (not_1_out, en);
  Multiplexer #(.width(32), .enable("false")) multiplexer_1 (
    .in0(I_PC), .in1({32{1'b0}}), .out(multiplexer_1_out), .sel(bubble));
  Multiplexer #(.width(32), .enable("false")) multiplexer_2 (
    .in0(I_IR), .in1({32{1'b0}}), .out(multiplexer_2_out), .sel(bubble));
  Multiplexer #(.enable("false")) multiplexer_3 (.in0(RegWrite), .in1(1'b0), .out(multiplexer_3_out), .sel(bubble));
  Multiplexer #(.enable("false")) multiplexer_4 (.in0(MemtoReg), .in1(1'b0), .out(multiplexer_4_out), .sel(bubble));
  Multiplexer #(.enable("false")) multiplexer_5 (.in0(MemWrite), .in1(1'b0), .out(multiplexer_5_out), .sel(bubble));
  Multiplexer #(.enable("false")) multiplexer_6 (.in0(SB), .in1(1'b0), .out(multiplexer_6_out), .sel(bubble));
  Multiplexer #(.enable("false")) multiplexer_7 (.in0(ALU_SRC), .in1(1'b0), .out(multiplexer_7_out), .sel(bubble));
  Multiplexer #(.enable("false")) multiplexer_8 (.in0(BEQ), .in1(1'b0), .out(multiplexer_8_out), .sel(bubble));
  Multiplexer #(.enable("false")) multiplexer_9 (.in0(BNE), .in1(1'b0), .out(multiplexer_9_out), .sel(bubble));
  Multiplexer #(.enable("false")) multiplexer_10 (.in0(JR), .in1(1'b0), .out(multiplexer_10_out), .sel(bubble));
  Multiplexer #(.enable("false")) multiplexer_11 (.in0(JMP), .in1(1'b0), .out(multiplexer_11_out), .sel(bubble));
  Multiplexer #(.enable("false")) multiplexer_12 (.in0(JAL), .in1(1'b0), .out(multiplexer_12_out), .sel(bubble));
  Multiplexer #(.enable("false")) multiplexer_13 (.in0(BGTZ), .in1(1'b0), .out(multiplexer_13_out), .sel(bubble));
  Multiplexer #(.enable("false")) multiplexer_14 (.in0(Shamt), .in1(1'b0), .out(multiplexer_14_out), .sel(bubble));
  Multiplexer #(.width(4), .enable("false")) multiplexer_15 (
    .in0(ALU_OP), .in1(4'b0000), .out(multiplexer_15_out), .sel(bubble));
  Multiplexer #(.enable("false")) multiplexer_16 (.in0(syscall), .in1(1'b0), .out(multiplexer_16_out), .sel(bubble));
  Multiplexer #(.width(5), .enable("false")) multiplexer_17 (
    .in0(W_num), .in1({5{1'b0}}), .out(multiplexer_17_out), .sel(bubble));
  Multiplexer #(.width(32), .enable("false")) multiplexer_18 (
    .in0(I_R1), .in1({32{1'b0}}), .out(multiplexer_18_out), .sel(bubble));
  Multiplexer #(.width(32), .enable("false")) multiplexer_19 (
    .in0(I_R2), .in1({32{1'b0}}), .out(multiplexer_19_out), .sel(bubble));
  Multiplexer #(.width(32), .enable("false")) multiplexer_20 (
    .in0(I_Imm), .in1({32{1'b0}}), .out(multiplexer_20_out), .sel(bubble));
  Multiplexer #(.width(4), .enable("false")) multiplexer_21 (
    .in0(sel), .in1(4'b0000), .out(multiplexer_21_out), .sel(bubble));
  Multiplexer #(.width(32), .enable("false")) multiplexer_22 (
    .in0(ExpAddr), .in1({32{1'b0}}), .out(multiplexer_22_out), .sel(bubble));
  Multiplexer #(.enable("false")) multiplexer_23 (.in0(\预测跳转 ), .in1(1'b0), .out(multiplexer_23_out), .sel(bubble));
  Register #(.width(32)) register_1 (.D(multiplexer_1_out), .en(not_1_out), .Q(O_PC), .clk(clk), .clr(clr));
  Register #(.width(32)) register_2 (.D(multiplexer_2_out), .en(not_1_out), .Q(O_IR), .clk(clk), .clr(clr));
  Register #(.width(1)) register_3 (.D(multiplexer_3_out), .en(not_1_out), .Q(RegWrite_2), .clk(clk), .clr(clr));
  Register #(.width(1)) register_4 (.D(multiplexer_4_out), .en(not_1_out), .Q(MemtoReg_2), .clk(clk), .clr(clr));
  Register #(.width(1)) register_5 (.D(multiplexer_5_out), .en(not_1_out), .Q(MemWrite_2), .clk(clk), .clr(clr));
  Register #(.width(1)) register_6 (.D(multiplexer_6_out), .en(not_1_out), .Q(SB_2), .clk(clk), .clr(clr));
  Register #(.width(1)) register_7 (.D(multiplexer_7_out), .en(not_1_out), .Q(ALU_SRC_2), .clk(clk), .clr(clr));
  Register #(.width(1)) register_8 (.D(multiplexer_8_out), .en(not_1_out), .Q(BEQ_2), .clk(clk), .clr(clr));
  Register #(.width(1)) register_9 (.D(multiplexer_9_out), .en(not_1_out), .Q(BNE_2), .clk(clk), .clr(clr));
  Register #(.width(1)) register_10 (.D(multiplexer_10_out), .en(not_1_out), .Q(JR_2), .clk(clk), .clr(clr));
  Register #(.width(1)) register_11 (.D(multiplexer_11_out), .en(not_1_out), .Q(JMP_2), .clk(clk), .clr(clr));
  Register #(.width(1)) register_12 (.D(multiplexer_12_out), .en(not_1_out), .Q(JAL_2), .clk(clk), .clr(clr));
  Register #(.width(1)) register_13 (.D(multiplexer_13_out), .en(not_1_out), .Q(BGTZ_2), .clk(clk), .clr(clr));
  Register #(.width(1)) register_14 (.D(multiplexer_14_out), .en(not_1_out), .Q(Shamt_2), .clk(clk), .clr(clr));
  Register #(.width(4)) register_15 (.D(multiplexer_15_out), .en(not_1_out), .Q(ALU_OP_2), .clk(clk), .clr(clr));
  Register #(.width(1)) register_16 (.D(multiplexer_16_out), .en(not_1_out), .Q(syscall_2), .clk(clk), .clr(clr));
  Register #(.width(5)) register_17 (.D(multiplexer_17_out), .en(not_1_out), .Q(W_num_2), .clk(clk), .clr(clr));
  Register #(.width(32)) register_18 (.D(multiplexer_18_out), .en(not_1_out), .Q(O_R1), .clk(clk), .clr(clr));
  Register #(.width(32)) register_19 (.D(multiplexer_19_out), .en(not_1_out), .Q(O_R2), .clk(clk), .clr(clr));
  Register #(.width(32)) register_20 (.D(multiplexer_20_out), .en(not_1_out), .Q(O_Imm), .clk(clk), .clr(clr));
  Register #(.width(4)) register_21 (.D(multiplexer_21_out), .en(not_1_out), .Q(sel_2), .clk(clk), .clr(clr));
  Register #(.width(32)) register_22 (.D(multiplexer_22_out), .en(not_1_out), .Q(ExpAddr_2), .clk(clk), .clr(clr));
  Register #(.width(1)) register_23 (.D(multiplexer_23_out), .en(not_1_out), .Q(\预测跳转_2 ), .clk(clk), .clr(clr));
endmodule

// EX/MEM
module EX_MEM (
  input  bubble,
  input  en,
  input  clk,
  input  clr,
  input  [31:0] I_PC,
  input  [31:0] I_IR,
  input  RegWrite,
  input  MemtoReg,
  input  MemWrite,
  input  JAL,
  input  Halt,
  input  [31:0] res1,
  input  [31:0] mem_din,
  input  [4:0] W_num,
  input  [3:0] sel,
  output [31:0] O_PC,
  output [31:0] O_IR,
  output RegWrite_2,
  output MemtoReg_2,
  output MemWrite_2,
  output JAL_2,
  output Halt_2,
  output [31:0] res1_2,
  output [31:0] mem_din_2,
  output [4:0] W_num_2,
  output [3:0] sel_2
);

  wire multiplexer_3_out, multiplexer_4_out, multiplexer_5_out, multiplexer_6_out, multiplexer_7_out,
       not_1_out;
  wire [3:0] multiplexer_11_out;
  wire [4:0] multiplexer_10_out;
  wire [31:0] multiplexer_1_out, multiplexer_2_out, multiplexer_8_out, multiplexer_9_out;

  not not_1 (not_1_out, en);
  Multiplexer #(.width(32), .enable("false")) multiplexer_1 (
    .in0(I_PC), .in1({32{1'b0}}), .out(multiplexer_1_out), .sel(bubble));
  Multiplexer #(.width(32), .enable("false")) multiplexer_2 (
    .in0(I_IR), .in1({32{1'b0}}), .out(multiplexer_2_out), .sel(bubble));
  Multiplexer #(.enable("false")) multiplexer_3 (.in0(RegWrite), .in1(1'b0), .out(multiplexer_3_out), .sel(bubble));
  Multiplexer #(.enable("false")) multiplexer_4 (.in0(MemtoReg), .in1(1'b0), .out(multiplexer_4_out), .sel(bubble));
  Multiplexer #(.enable("false")) multiplexer_5 (.in0(MemWrite), .in1(1'b0), .out(multiplexer_5_out), .sel(bubble));
  Multiplexer #(.enable("false")) multiplexer_6 (.in0(JAL), .in1(1'b0), .out(multiplexer_6_out), .sel(bubble));
  Multiplexer #(.enable("false")) multiplexer_7 (.in0(Halt), .in1(1'b0), .out(multiplexer_7_out), .sel(bubble));
  Multiplexer #(.width(32), .enable("false")) multiplexer_8 (
    .in0(res1), .in1({32{1'b0}}), .out(multiplexer_8_out), .sel(bubble));
  Multiplexer #(.width(32), .enable("false")) multiplexer_9 (
    .in0(mem_din), .in1({32{1'b0}}), .out(multiplexer_9_out), .sel(bubble));
  Multiplexer #(.width(5), .enable("false")) multiplexer_10 (
    .in0(W_num), .in1({5{1'b0}}), .out(multiplexer_10_out), .sel(bubble));
  Multiplexer #(.width(4), .enable("false")) multiplexer_11 (
    .in0(sel), .in1(4'b0000), .out(multiplexer_11_out), .sel(bubble));
  Register #(.width(32)) register_1 (.D(multiplexer_1_out), .en(not_1_out), .Q(O_PC), .clk(clk), .clr(clr));
  Register #(.width(32)) register_2 (.D(multiplexer_2_out), .en(not_1_out), .Q(O_IR), .clk(clk), .clr(clr));
  Register #(.width(1)) register_3 (.D(multiplexer_3_out), .en(not_1_out), .Q(RegWrite_2), .clk(clk), .clr(clr));
  Register #(.width(1)) register_4 (.D(multiplexer_4_out), .en(not_1_out), .Q(MemtoReg_2), .clk(clk), .clr(clr));
  Register #(.width(1)) register_5 (.D(multiplexer_5_out), .en(not_1_out), .Q(MemWrite_2), .clk(clk), .clr(clr));
  Register #(.width(1)) register_6 (.D(multiplexer_6_out), .en(not_1_out), .Q(JAL_2), .clk(clk), .clr(clr));
  Register #(.width(1)) register_7 (.D(multiplexer_7_out), .en(not_1_out), .Q(Halt_2), .clk(clk), .clr(clr));
  Register #(.width(32)) register_8 (.D(multiplexer_8_out), .en(not_1_out), .Q(res1_2), .clk(clk), .clr(clr));
  Register #(.width(32)) register_9 (.D(multiplexer_9_out), .en(not_1_out), .Q(mem_din_2), .clk(clk), .clr(clr));
  Register #(.width(5)) register_10 (.D(multiplexer_10_out), .en(not_1_out), .Q(W_num_2), .clk(clk), .clr(clr));
  Register #(.width(4)) register_11 (.D(multiplexer_11_out), .en(not_1_out), .Q(sel_2), .clk(clk), .clr(clr));
endmodule

// MEM/WB
module MEM_WB (
  input  bubble,
  input  en,
  input  clk,
  input  clr,
  input  [31:0] I_PC,
  input  [31:0] I_IR,
  input  RegWrite,
  input  MemtoReg,
  input  jal,
  input  [31:0] res1,
  input  [31:0] MemOut,
  input  [4:0] W_num,
  output [31:0] O_PC,
  output [31:0] O_IR,
  output RegWrite_2,
  output MemtoReg_2,
  output jal_2,
  output [31:0] res1_2,
  output [31:0] MemOut_2,
  output [4:0] W_num_2
);

  wire multiplexer_3_out, multiplexer_4_out, multiplexer_5_out, not_1_out;
  wire [4:0] multiplexer_8_out;
  wire [31:0] multiplexer_1_out, multiplexer_2_out, multiplexer_6_out, multiplexer_7_out;

  not not_1 (not_1_out, en);
  Multiplexer #(.width(32), .enable("false")) multiplexer_1 (
    .in0(I_PC), .in1({32{1'b0}}), .out(multiplexer_1_out), .sel(bubble));
  Multiplexer #(.width(32), .enable("false")) multiplexer_2 (
    .in0(I_IR), .in1({32{1'b0}}), .out(multiplexer_2_out), .sel(bubble));
  Multiplexer #(.enable("false")) multiplexer_3 (.in0(RegWrite), .in1(1'b0), .out(multiplexer_3_out), .sel(bubble));
  Multiplexer #(.enable("false")) multiplexer_4 (.in0(MemtoReg), .in1(1'b0), .out(multiplexer_4_out), .sel(bubble));
  Multiplexer #(.enable("false")) multiplexer_5 (.in0(jal), .in1(1'b0), .out(multiplexer_5_out), .sel(bubble));
  Multiplexer #(.width(32), .enable("false")) multiplexer_6 (
    .in0(res1), .in1({32{1'b0}}), .out(multiplexer_6_out), .sel(bubble));
  Multiplexer #(.width(32), .enable("false")) multiplexer_7 (
    .in0(MemOut), .in1({32{1'b0}}), .out(multiplexer_7_out), .sel(bubble));
  Multiplexer #(.width(5), .enable("false")) multiplexer_8 (
    .in0(W_num), .in1({5{1'b0}}), .out(multiplexer_8_out), .sel(bubble));
  Register #(.width(32)) register_1 (.D(multiplexer_1_out), .en(not_1_out), .Q(O_PC), .clk(clk), .clr(clr));
  Register #(.width(32)) register_2 (.D(multiplexer_2_out), .en(not_1_out), .Q(O_IR), .clk(clk), .clr(clr));
  Register #(.width(1)) register_3 (.D(multiplexer_3_out), .en(not_1_out), .Q(RegWrite_2), .clk(clk), .clr(clr));
  Register #(.width(1)) register_4 (.D(multiplexer_4_out), .en(not_1_out), .Q(MemtoReg_2), .clk(clk), .clr(clr));
  Register #(.width(1)) register_5 (.D(multiplexer_5_out), .en(not_1_out), .Q(jal_2), .clk(clk), .clr(clr));
  Register #(.width(32)) register_6 (.D(multiplexer_6_out), .en(not_1_out), .Q(res1_2), .clk(clk), .clr(clr));
  Register #(.width(32)) register_7 (.D(multiplexer_7_out), .en(not_1_out), .Q(MemOut_2), .clk(clk), .clr(clr));
  Register #(.width(5)) register_8 (.D(multiplexer_8_out), .en(not_1_out), .Q(W_num_2), .clk(clk), .clr(clr));
endmodule

module \分支相关流水线  (
  output [31:0] out_1
);

  wire AluSrcB, and_1_out, and_2_out, and_3_out, and_4_out, and_5_out, and_6_out, and_7_out, Beq, BGTZ, Bne,
       bubble1, CLK, comparator_1_eq, comparator_2_gt, EN, ex_mem_1_p18, ex_mem_1_p19, ex_mem_1_p20,
       ex_mem_1_p21, ex_mem_1_p22, ex_mem_1_p23, Go, id_ex_1_alu_src_2, id_ex_1_beq_2, id_ex_1_bgtz_2,
       id_ex_1_bne_2, id_ex_1_jal_2, id_ex_1_jmp_2, id_ex_1_jr_2, id_ex_1_memtoreg_2, id_ex_1_memwrite_2,
       id_ex_1_regwrite_2, id_ex_1_sb_2, id_ex_1_shamt_2, IR1, IR2, IR3, JAL, JMP, JR, MemToReg, MemWrite,
       mips_alu_1_equal, mips_probe_1_p1, not_2_out, or_4_out, or_5_out, RegDst, register_2_q, RegWrite,
       RegWrite_num, RST, run, SB, Shamt, SignedExt, Syscall, Syscall_num, W1, W2, W3;
  wire [1:0] ex_mem_1_p24, PCSrc;
  wire [3:0] AluOP, decoder_1_out0, id_ex_1_alu_op_2, multiplexer_10_out;
  wire [4:0] ex_mem_1_p26, id_ex_1_w_num_2, mem_wb_1_w_num_2, multiplexer_2_out, multiplexer_3_out,
       multiplexer_4_out, multiplexer_5_out, multiplexer_8_out;
  wire [15:0] \LoadUse次数 , \总周期数 , \插入气泡数 , \无条件分支数 , \条件分支成功数 ;
  wire [31:0] adder_1_out, adder_2_out, adder_3_out, adder_4_out, bit_extender_1_out, bit_extender_2_out,
       ex_mem_1_p17, ex_mem_1_p25, EX_PC, id_ex_1_o_imm, id_ex_1_o_ir, id_ex_1_o_r1, id_ex_1_o_r2, ID_PC,
       IF_PC, LedData, MEM_PC, mem_wb_1_memout_2, mips_alu_1_result, mips_ram_1_p8, mips_regifile_1_r1,
       mips_regifile_1_r2, multiplexer_1_out, multiplexer_6_out, multiplexer_7_out, multiplexer_9_out,
       multiplexer_11_out, multiplexer_12_out, rom_1_data, shifter_1_out, WB_PC;
  wire [31:2] ex_mem_1_p24_2;

  Button \u_总复位  (.out(RST));
  Button _1 (.out(IR1));
  Button _2 (.out(IR2));
  Button _3 (.out(IR3));
  Button \u_继续运行  (.out(Go));
  LED led_1 (.in(W1));
  LED led_2 (.in(W2));
  LED led_3 (.in(W3));
  Multiplexer #(.select(2), .width(32), .enable("false")) multiplexer_1 (
    .in0(adder_1_out), .in1(adder_3_out), .in2({adder_2_out[31:28], id_ex_1_o_ir[25:0], 2'b00}),
    .in3(id_ex_1_o_r1), .out(multiplexer_1_out), .sel(PCSrc));
  Hex_Digit_Display hex_digit_display_1 (.value(LedData[31:28]));  // open: dp
  Register #(.width(32)) PC (.D(multiplexer_1_out), .en(run), .Q(IF_PC), .clk(CLK), .clr(RST));
  Hex_Digit_Display hex_digit_display_2 (.value(LedData[23:20]));  // open: dp
  Hex_Digit_Display hex_digit_display_3 (.value(LedData[27:24]));  // open: dp
  not not_1 (EN, run);
  or or_1 (bubble1, PCSrc[1], PCSrc[0]);
  Hex_Digit_Display hex_digit_display_4 (.value(LedData[15:12]));  // open: dp
  Hex_Digit_Display hex_digit_display_5 (.value(LedData[19:16]));  // open: dp
  Counter #(.width(16), .max('hffff)) counter_1 (
    .count(run), .Q(\总周期数 ), .clk(CLK), .clr(RST));  // open: load, D, carry
  Hex_Digit_Display hex_digit_display_6 (.value(LedData[7:4]));  // open: dp
  Hex_Digit_Display hex_digit_display_7 (.value(LedData[11:8]));  // open: dp
  Clock clock_1 (.out(CLK));
  ROM #(.addrWidth(24), .dataWidth(32)) rom_1 (.addr(IF_PC[25:2]), .data(rom_1_data));  // open: sel
  Adder #(.width(32)) adder_1 (.a(IF_PC), .b(32'h4), .out(adder_1_out));  // open: cin, cout
  Hex_Digit_Display hex_digit_display_8 (.value(LedData[3:0]));  // open: dp
  IF_ID if_id_1 (
    .I_PC(IF_PC), .I_IR(rom_1_data), .O_PC(ID_PC), .O_IR(out_1), .bubble(bubble1), .en(EN), .clk(CLK),
    .clr(RST));  // open: ExpAddr, ExpAddr_2, 预测跳转, 预测跳转_2
  // Probe on \总周期数 
  // Probe on \无条件分支数 
  // Probe on \条件分支成功数 
  // Probe on \插入气泡数 
  // Probe on \LoadUse次数 
  Multiplexer #(.width(5), .enable("false")) multiplexer_2 (
    .in0(out_1[20:16]), .in1(out_1[15:11]), .out(multiplexer_2_out), .sel(RegDst));
  // Probe on IF_PC[11:0]
  Multiplexer #(.width(5), .enable("false")) multiplexer_3 (
    .in0(out_1[25:21]), .in1(5'b00010), .out(multiplexer_3_out), .sel(Syscall));
  Multiplexer #(.width(5), .enable("false")) multiplexer_4 (
    .in0(out_1[20:16]), .in1(5'b00100), .out(multiplexer_4_out), .sel(Syscall));
  Multiplexer #(.width(5), .enable("false")) multiplexer_5 (
    .in0(multiplexer_2_out), .in1({5{1'b1}}), .out(multiplexer_5_out), .sel(JAL));
  assign bit_extender_1_out = {{16{out_1[15]}}, out_1[15:0]};  // Bit_Extender bit_extender_1
  assign bit_extender_2_out = {{16{1'b0}}, out_1[15:0]};  // Bit_Extender bit_extender_2
  // Probe on ID_PC[11:0]
  // Probe on EX_PC[11:0]
  // Probe on MEM_PC[11:0]
  MIPS_Regifile mips_regifile_1 (
    .Din(mem_wb_1_memout_2), .Clk(CLK), .R1(mips_regifile_1_r1), .R2(mips_regifile_1_r2), .WE(RegWrite_num),
    .W_num(mem_wb_1_w_num_2), .R1_num(multiplexer_3_out), .R2_num(multiplexer_4_out));
  Multiplexer #(.width(32), .enable("false")) multiplexer_6 (
    .in0(bit_extender_2_out), .in1(bit_extender_1_out), .out(multiplexer_6_out), .sel(SignedExt));
  // Probe on WB_PC[11:0]
  ID_EX id_ex_1 (
    .I_PC(ID_PC), .I_IR(out_1), .RegWrite(RegWrite), .MemtoReg(MemToReg), .MemWrite(MemWrite), .SB(SB),
    .ALU_SRC(AluSrcB), .BEQ(Beq), .BNE(Bne), .JR(JR), .JMP(JMP), .JAL(JAL), .BGTZ(BGTZ), .Shamt(Shamt),
    .ALU_OP(AluOP), .syscall(Syscall), .O_PC(EX_PC), .O_IR(id_ex_1_o_ir), .RegWrite_2(id_ex_1_regwrite_2),
    .MemtoReg_2(id_ex_1_memtoreg_2), .MemWrite_2(id_ex_1_memwrite_2), .SB_2(id_ex_1_sb_2),
    .ALU_SRC_2(id_ex_1_alu_src_2), .BEQ_2(id_ex_1_beq_2), .BNE_2(id_ex_1_bne_2), .JR_2(id_ex_1_jr_2),
    .JMP_2(id_ex_1_jmp_2), .JAL_2(id_ex_1_jal_2), .BGTZ_2(id_ex_1_bgtz_2), .Shamt_2(id_ex_1_shamt_2),
    .ALU_OP_2(id_ex_1_alu_op_2), .syscall_2(Syscall_num), .bubble(bubble1), .en(EN), .clk(CLK), .clr(RST),
    .I_R1(mips_regifile_1_r1), .I_R2(mips_regifile_1_r2), .O_R1(id_ex_1_o_r1), .O_R2(id_ex_1_o_r2),
    .I_Imm(multiplexer_6_out), .O_Imm(id_ex_1_o_imm), .W_num(multiplexer_5_out), .W_num_2(id_ex_1_w_num_2));  // open: sel, sel_2, ExpAddr, ExpAddr_2, 预测跳转, 预测跳转_2
  // MIPS_Probe mips_probe_1: pin names not known; wires that end beside it: mips_probe_1_p1, id_ex_1_o_ir
  Adder #(.width(32)) adder_2 (.a(EX_PC), .b(32'h4), .out(adder_2_out));  // open: cin, cout
  Shifter #(.width(32)) shifter_1 (.in(id_ex_1_o_imm), .\dist (5'b00010), .out(shifter_1_out));
  \硬布线控制器  \u_硬布线控制器_1  (
    .Func(out_1[5:0]), .OP(out_1[31:26]), .ALU_OP(AluOP), .MemToReg(MemToReg), .MemWrite(MemWrite),
    .ALU_SRC(AluSrcB), .RegWrite(RegWrite), .SysCALL(Syscall), .SignedExt(SignedExt), .RegDst(RegDst),
    .JR(JR), .JMP(JMP), .Beq(Beq), .Bne(Bne), .JAL(JAL), .SHAMT(Shamt), .SB(SB), .BGTZ(BGTZ));
  Adder #(.width(32)) adder_3 (.a(adder_2_out), .b(shifter_1_out), .out(adder_3_out));  // open: cin, cout
  and and_1 (and_1_out, ~comparator_1_eq, Syscall_num);  // AND_Gate
  and and_2 (and_2_out, comparator_1_eq, Syscall_num);
  Comparator #(.width(32)) comparator_1 (.a(32'h22), .b(id_ex_1_o_r1), .eq(comparator_1_eq));  // open: gt, lt
  Multiplexer #(.width(32), .disabled(0), .enable("false")) multiplexer_7 (
    .in0(id_ex_1_o_r2), .in1(id_ex_1_o_imm), .out(multiplexer_7_out), .sel(id_ex_1_alu_src_2));
  Register #(.width(32)) register_1 (.D(id_ex_1_o_r2), .en(and_2_out), .Q(LedData), .clk(CLK), .clr(RST));
  Multiplexer #(.width(5), .enable("false")) multiplexer_8 (
    .in0(id_ex_1_o_r1[4:0]), .in1(id_ex_1_o_ir[10:6]), .out(multiplexer_8_out), .sel(id_ex_1_shamt_2));
  Comparator #(.width(32)) comparator_2 (.a(id_ex_1_o_r1), .b({32{1'b0}}), .gt(comparator_2_gt));  // open: eq, lt
  MIPS_ALU mips_alu_1 (
    .X(id_ex_1_o_r1), .Y(multiplexer_7_out), .AluOP(id_ex_1_alu_op_2), .Equal(mips_alu_1_equal),
    .Result(mips_alu_1_result), .shamt(multiplexer_8_out));  // open: Result_2
  and and_3 (and_3_out, comparator_2_gt, id_ex_1_bgtz_2);
  not not_2 (not_2_out, mips_alu_1_equal);
  and and_4 (and_4_out, not_2_out, id_ex_1_bne_2);
  and and_5 (and_5_out, mips_alu_1_equal, id_ex_1_beq_2);
  and and_6 (and_6_out, run, PCSrc[1]);
  Counter #(.width(16), .max('hffff)) counter_2 (
    .count(and_6_out), .Q(\无条件分支数 ), .clk(CLK), .clr(RST));  // open: load, D, carry
  or or_2 (PCSrc[1], id_ex_1_jal_2, id_ex_1_jmp_2, id_ex_1_jr_2);
  or or_3 (PCSrc[0], id_ex_1_jr_2, and_4_out, and_5_out, and_3_out);
  Counter #(.width(16), .max('hffff)) counter_3 (
    .count(and_7_out), .Q(\条件分支成功数 ), .clk(CLK), .clr(RST));  // open: load, D, carry
  and and_7 (and_7_out, run, or_4_out);
  or or_4 (or_4_out, and_4_out, and_5_out, and_3_out);
  // EX_MEM ex_mem_1: pin names not known; wires that end beside it: EX_PC, id_ex_1_o_ir, id_ex_1_regwrite_2, id_ex_1_memtoreg_2, id_ex_1_memwrite_2, id_ex_1_sb_2, id_ex_1_jal_2, and_1_out, mips_alu_1_result, id_ex_1_o_r2, id_ex_1_w_num_2, 1'b0, EN, CLK, RST, MEM_PC, ex_mem_1_p17, ex_mem_1_p18, ex_mem_1_p19, ex_mem_1_p20, ex_mem_1_p21, ex_mem_1_p22, ex_mem_1_p23, {ex_mem_1_p24_2, ex_mem_1_p24}, ex_mem_1_p25, ex_mem_1_p26
  not not_3 (run, register_2_q);
  Register #(.width(1)) register_2 (.D(1'b1), .en(ex_mem_1_p23), .Q(register_2_q), .clk(CLK), .clr(or_5_out));
  or or_5 (or_5_out, RST, Go);
  Decoder #(.select(2), .enable("false")) decoder_1 (
    .out0(decoder_1_out0[0]), .out1(decoder_1_out0[1]), .out2(decoder_1_out0[2]), .out3(decoder_1_out0[3]),
    .sel(ex_mem_1_p24));
  Adder #(.width(32)) adder_4 (.a(MEM_PC), .b(32'h4), .out(adder_4_out));  // open: cin, cout
  Multiplexer #(.width(32), .enable("false")) multiplexer_9 (
    .in0(ex_mem_1_p25), .in1({ex_mem_1_p25[7:0], ex_mem_1_p25[7:0], ex_mem_1_p25[7:0], ex_mem_1_p25[7:0]}),
    .out(multiplexer_9_out), .sel(ex_mem_1_p21));
  Multiplexer #(.width(4), .enable("false")) multiplexer_10 (
    .in0(4'b1111), .in1(decoder_1_out0), .out(multiplexer_10_out), .sel(ex_mem_1_p21));
  Multiplexer #(.width(32), .enable("false")) multiplexer_11 (
    .in0({ex_mem_1_p24_2, ex_mem_1_p24}), .in1(mips_ram_1_p8), .out(multiplexer_11_out), .sel(ex_mem_1_p19));
  // MIPS_RAM mips_ram_1: pin names not known; wires that end beside it: ex_mem_1_p24_2[25:2], multiplexer_9_out, ex_mem_1_p20, multiplexer_10_out, CLK, 1'b1, RST, mips_ram_1_p8
  Multiplexer #(.width(32), .enable("false")) multiplexer_12 (
    .in0(multiplexer_11_out), .in1(adder_4_out), .out(multiplexer_12_out), .sel(ex_mem_1_p22));
  MEM_WB mem_wb_1 (
    .I_PC(MEM_PC), .I_IR(ex_mem_1_p17), .RegWrite(ex_mem_1_p18), .W_num(ex_mem_1_p26), .O_PC(WB_PC),
    .RegWrite_2(RegWrite_num), .W_num_2(mem_wb_1_w_num_2), .bubble(1'b0), .en(EN), .clk(CLK), .clr(RST),
    .MemOut(multiplexer_12_out), .MemOut_2(mem_wb_1_memout_2));  // open: O_IR, res1, res1_2, MemtoReg, MemtoReg_2, jal, jal_2

  // Other names for the same wires on the sheet: bubble2 = bubble1; Func[5:0] = out_1[5:0]; Op[5:0] = out_1[31:26];
  //   PC[31:0] = IF_PC

  // Notes on the sheet:
  //   中断源
  //   中断等待指示
  //   数码管输出
  //   syscall: if $v0(2) == 34 then print $a0(4) else pause
  //   指令存储器
  //   contents of rom_1 (hex, n*v repeats v):
  //   20110100 20020022 8000006 20110004 20120005 20130006 10000003 20110007 20120008 20130009 14110003
  //   2011000a 2012000b 2013000c c000014 2002000a 0 0 0 c 2231ffff 0 0 0 112020 0 0 0 c 1620fff6 3e00008
  //   指令字
  //   OP
  //   Func
  //   rs
  //   rt
  //   rd
  //   流水调试日志用
endmodule

module \气泡流水线  (
  output [4:0] out_1,
  output [31:0] out_2
);

  wire AluSrcB, and_1_out, and_2_out, and_3_out, and_4_out, and_5_out, and_6_out, and_7_out, and_8_out,
       and_9_out, Beq, BGTZ, Bne, bubble1, bubble2, CLK, comparator_1_eq, comparator_2_gt, Data_Relate, EN1,
       EN2, ex_mem_1_halt_2, ex_mem_1_jal_2, ex_mem_1_memtoreg_2, ex_mem_1_memwrite_2, EX_RegWrite, Go,
       id_ex_1_alu_src_2, id_ex_1_beq_2, id_ex_1_bgtz_2, id_ex_1_bne_2, id_ex_1_jal_2, id_ex_1_jmp_2,
       id_ex_1_jr_2, id_ex_1_memtoreg_2, id_ex_1_memwrite_2, id_ex_1_sb_2, id_ex_1_shamt_2, IR1, IR2, IR3,
       JAL, JMP, JR, MEM_RegWrite, mem_wb_1_jal_2, mem_wb_1_memtoreg_2, MemToReg, MemWrite, mips_alu_1_equal,
       not_2_out, not_3_out, or_6_out, or_7_out, RegDst, register_2_q, RegWrite, RST, run, SB, Shamt,
       SignedExt, Syscall, Syscall_num, W1, W2, W3, WB_RegWrite;
  wire [1:0] PCSrc;
  wire [3:0] AluOP, decoder_1_out0, ex_mem_1_sel_2, id_ex_1_alu_op_2, multiplexer_10_out;
  wire [4:0] EX_RegWrite_num, ID_R1_num, MEM_RegWrite_num, mem_wb_1_w_num_2, multiplexer_2_out,
       multiplexer_3_out, multiplexer_8_out;
  wire [15:0] \LoadUse次数 , \总周期数 , \插入气泡数 , \无条件分支数 , \条件分支成功数 ;
  wire [27:0] adder_2_out;
  wire [31:0] adder_1_out, adder_3_out, adder_4_out, bit_extender_1_out, bit_extender_2_out,
       ex_mem_1_mem_din_2, ex_mem_1_o_ir, ex_mem_1_res1_2, EX_PC, id_ex_1_o_imm, id_ex_1_o_r1, id_ex_1_o_r2,
       ID_PC, IF_PC, LedData, MEM_PC, mem_wb_1_memout_2, mem_wb_1_res1_2, mips_alu_1_result, mips_ram_1_p8,
       mips_regifile_1_r1, mips_regifile_1_r2, multiplexer_1_out, multiplexer_6_out, multiplexer_7_out,
       multiplexer_9_out, multiplexer_11_out, multiplexer_12_out, rom_1_data, shifter_1_out, WB_PC;
  wire [31:2] adder_2_out_2;
  wire [31:26] id_ex_1_o_ir;

  Button \u_总复位  (.out(RST));
  Button _1 (.out(IR1));
  Button _2 (.out(IR2));
  Button _3 (.out(IR3));
  Button \u_继续运行  (.out(Go));
  LED led_1 (.in(W1));
  LED led_2 (.in(W2));
  LED led_3 (.in(W3));
  not not_1 (EN2, run);
  not not_2 (not_2_out, Data_Relate);
  Hex_Digit_Display hex_digit_display_1 (.value(LedData[31:28]));  // open: dp
  and and_1 (and_1_out, Data_Relate, run);
  and and_2 (and_2_out, not_2_out, run);
  Register #(.width(32)) PC (.D(multiplexer_1_out), .en(and_2_out), .Q(IF_PC), .clk(CLK), .clr(RST));
  Multiplexer #(.select(2), .width(32), .enable("false")) multiplexer_1 (
    .in0(adder_1_out), .in1(adder_3_out), .in2({adder_2_out_2, 2'b00}), .in3(id_ex_1_o_r1),
    .out(multiplexer_1_out), .sel(PCSrc));
  Hex_Digit_Display hex_digit_display_2 (.value(LedData[27:24]));  // open: dp
  Hex_Digit_Display hex_digit_display_3 (.value(LedData[23:20]));  // open: dp
  or or_1 (EN1, Data_Relate, EN2);
  or or_2 (bubble1, PCSrc[1], PCSrc[0]);
  Counter #(.width(16), .max('hffff)) counter_1 (
    .count(and_1_out), .Q(\插入气泡数 ), .clk(CLK), .clr(RST));  // open: load, D, carry
  Hex_Digit_Display hex_digit_display_4 (.value(LedData[15:12]));  // open: dp
  Hex_Digit_Display hex_digit_display_5 (.value(LedData[19:16]));  // open: dp
  or or_3 (bubble2, bubble1, Data_Relate);
  Counter #(.width(16), .max('hffff)) counter_2 (
    .count(run), .Q(\总周期数 ), .clk(CLK), .clr(RST));  // open: load, D, carry
  Hex_Digit_Display hex_digit_display_6 (.value(LedData[11:8]));  // open: dp
  Hex_Digit_Display hex_digit_display_7 (.value(LedData[7:4]));  // open: dp
  Clock clock_1 (.out(CLK));
  Adder #(.width(32)) adder_1 (.a(IF_PC), .b(32'h4), .out(adder_1_out));  // open: cin, cout
  Hex_Digit_Display hex_digit_display_8 (.value(LedData[3:0]));  // open: dp
  ROM #(.addrWidth(24), .dataWidth(32)) rom_1 (.addr(IF_PC[25:2]), .data(rom_1_data));  // open: sel
  IF_ID if_id_1 (
    .I_PC(IF_PC), .I_IR(rom_1_data), .O_PC(ID_PC), .O_IR(out_2), .bubble(bubble1), .en(EN1), .clk(CLK),
    .clr(RST));  // open: ExpAddr, ExpAddr_2, 预测跳转, 预测跳转_2
  // Probe on \总周期数 
  // Probe on \无条件分支数 
  // Probe on \条件分支成功数 
  // Probe on \插入气泡数 
  // Probe on \LoadUse次数 
  // Probe on IF_PC[11:0]
  Multiplexer #(.width(5), .enable("false")) multiplexer_2 (
    .in0(out_2[20:16]), .in1(out_2[15:11]), .out(multiplexer_2_out), .sel(RegDst));
  Multiplexer #(.width(5), .enable("false")) multiplexer_3 (
    .in0(multiplexer_2_out), .in1({5{1'b1}}), .out(multiplexer_3_out), .sel(JAL));
  assign bit_extender_1_out = {{16{out_2[15]}}, out_2[15:0]};  // Bit_Extender bit_extender_1
  assign bit_extender_2_out = {{16{1'b0}}, out_2[15:0]};  // Bit_Extender bit_extender_2
  // Probe on ID_PC[11:0]
  \数据相关检测  \u_数据相关检测_1  (
    .OP(out_2[31:26]), .EX_WriteReg_num(EX_RegWrite_num), .EX_RegWrite(EX_RegWrite),
    .MEM_WriteReg_num(MEM_RegWrite_num), .MEM_RegWrite(MEM_RegWrite), .\数据相关 (Data_Relate),
    .Func(out_2[5:0]), .ID_R1_num(ID_R1_num), .ID_R2_num(out_1));
  Multiplexer #(.width(5), .enable("false")) multiplexer_4 (
    .in0(out_2[25:21]), .in1(5'b00010), .out(ID_R1_num), .sel(Syscall));
  Multiplexer #(.width(5), .enable("false")) multiplexer_5 (
    .in0(out_2[20:16]), .in1(5'b00100), .out(out_1), .sel(Syscall));
  // Probe on EX_PC[11:0]
  // Probe on MEM_PC[11:0]
  MIPS_Regifile mips_regifile_1 (
    .Din(multiplexer_12_out), .Clk(CLK), .R1(mips_regifile_1_r1), .R2(mips_regifile_1_r2), .WE(WB_RegWrite),
    .W_num(mem_wb_1_w_num_2), .R1_num(ID_R1_num), .R2_num(out_1));
  Multiplexer #(.width(32), .enable("false")) multiplexer_6 (
    .in0(bit_extender_2_out), .in1(bit_extender_1_out), .out(multiplexer_6_out), .sel(SignedExt));
  // Probe on WB_PC[11:0]
  ID_EX id_ex_1 (
    .I_PC(ID_PC), .I_IR(out_2), .RegWrite(RegWrite), .MemtoReg(MemToReg), .MemWrite(MemWrite), .SB(SB),
    .ALU_SRC(AluSrcB), .BEQ(Beq), .BNE(Bne), .JR(JR), .JMP(JMP), .JAL(JAL), .BGTZ(BGTZ), .Shamt(Shamt),
    .ALU_OP(AluOP), .syscall(Syscall), .O_PC(EX_PC), .O_IR({id_ex_1_o_ir, adder_2_out_2[27:2]}),
    .RegWrite_2(EX_RegWrite), .MemtoReg_2(id_ex_1_memtoreg_2), .MemWrite_2(id_ex_1_memwrite_2),
    .SB_2(id_ex_1_sb_2), .ALU_SRC_2(id_ex_1_alu_src_2), .BEQ_2(id_ex_1_beq_2), .BNE_2(id_ex_1_bne_2),
    .JR_2(id_ex_1_jr_2), .JMP_2(id_ex_1_jmp_2), .JAL_2(id_ex_1_jal_2), .BGTZ_2(id_ex_1_bgtz_2),
    .Shamt_2(id_ex_1_shamt_2), .ALU_OP_2(id_ex_1_alu_op_2), .syscall_2(Syscall_num), .bubble(bubble2),
    .en(EN2), .clk(CLK), .clr(RST), .I_R1(mips_regifile_1_r1), .I_R2(mips_regifile_1_r2),
    .O_R1(id_ex_1_o_r1), .O_R2(id_ex_1_o_r2), .I_Imm(multiplexer_6_out), .O_Imm(id_ex_1_o_imm),
    .W_num(multiplexer_3_out), .W_num_2(EX_RegWrite_num));  // open: sel, sel_2, ExpAddr, ExpAddr_2, 预测跳转, 预测跳转_2
  // MIPS_Probe mips_probe_1: pin names not known; wires that end beside it: out_2
  Adder #(.width(32)) adder_2 (.a(EX_PC), .b(32'h4), .out({adder_2_out_2[31:28], adder_2_out}));  // open: cin, cout
  Shifter #(.width(32)) shifter_1 (.in(id_ex_1_o_imm), .\dist (5'b00010), .out(shifter_1_out));
  \硬布线控制器  \u_硬布线控制器_1  (
    .Func(out_2[5:0]), .OP(out_2[31:26]), .ALU_OP(AluOP), .MemToReg(MemToReg), .MemWrite(MemWrite),
    .ALU_SRC(AluSrcB), .RegWrite(RegWrite), .SysCALL(Syscall), .SignedExt(SignedExt), .RegDst(RegDst),
    .JR(JR), .JMP(JMP), .Beq(Beq), .Bne(Bne), .JAL(JAL), .SHAMT(Shamt), .SB(SB), .BGTZ(BGTZ));
  Adder #(.width(32)) adder_3 (
    .a({adder_2_out_2[31:28], adder_2_out}), .b(shifter_1_out), .out(adder_3_out));  // open: cin, cout
  Comparator #(.width(32)) comparator_1 (.a(32'h22), .b(id_ex_1_o_r1), .eq(comparator_1_eq));  // open: gt, lt
  Multiplexer #(.width(32), .disabled(0), .enable("false")) multiplexer_7 (
    .in0(id_ex_1_o_r2), .in1(id_ex_1_o_imm), .out(multiplexer_7_out), .sel(id_ex_1_alu_src_2));
  and and_3 (and_3_out, ~comparator_1_eq, Syscall_num);  // AND_Gate
  and and_4 (and_4_out, comparator_1_eq, Syscall_num);
  Register #(.width(32)) register_1 (.D(id_ex_1_o_r2), .en(and_4_out), .Q(LedData), .clk(CLK), .clr(RST));
  MIPS_ALU mips_alu_1 (
    .X(id_ex_1_o_r1), .Y(multiplexer_7_out), .AluOP(id_ex_1_alu_op_2), .Equal(mips_alu_1_equal),
    .Result(mips_alu_1_result), .shamt(multiplexer_8_out));  // open: Result_2
  Multiplexer #(.width(5), .enable("false")) multiplexer_8 (
    .in0(id_ex_1_o_r1[4:0]), .in1(adder_2_out_2[12:8]), .out(multiplexer_8_out), .sel(id_ex_1_shamt_2));
  Comparator #(.width(32)) comparator_2 (.a(id_ex_1_o_r1), .b({32{1'b0}}), .gt(comparator_2_gt));  // open: eq, lt
  not not_3 (not_3_out, mips_alu_1_equal);
  and and_5 (and_5_out, not_3_out, id_ex_1_bne_2);
  and and_6 (and_6_out, mips_alu_1_equal, id_ex_1_beq_2);
  and and_7 (and_7_out, comparator_2_gt, id_ex_1_bgtz_2);
  Counter #(.width(16), .max('hffff)) counter_3 (
    .count(and_8_out), .Q(\无条件分支数 ), .clk(CLK), .clr(RST));  // open: load, D, carry
  and and_8 (and_8_out, run, PCSrc[1]);
  or or_4 (PCSrc[1], id_ex_1_jal_2, id_ex_1_jmp_2, id_ex_1_jr_2);
  or or_5 (PCSrc[0], id_ex_1_jr_2, and_5_out, and_6_out, and_7_out);
  Counter #(.width(16), .max('hffff)) counter_4 (
    .count(and_9_out), .Q(\条件分支成功数 ), .clk(CLK), .clr(RST));  // open: load, D, carry
  and and_9 (and_9_out, run, or_6_out);
  or or_6 (or_6_out, and_5_out, and_6_out, and_7_out);
  Decoder #(.select(2), .enable("false")) decoder_1 (
    .out0(decoder_1_out0[0]), .out1(decoder_1_out0[1]), .out2(decoder_1_out0[2]), .out3(decoder_1_out0[3]),
    .sel(mips_alu_1_result[1:0]));
  Multiplexer #(.width(32), .enable("false")) multiplexer_9 (
    .in0(id_ex_1_o_r2), .in1({id_ex_1_o_r2[7:0], id_ex_1_o_r2[7:0], id_ex_1_o_r2[7:0], id_ex_1_o_r2[7:0]}),
    .out(multiplexer_9_out), .sel(id_ex_1_sb_2));
  Multiplexer #(.width(4), .enable("false")) multiplexer_10 (
    .in0(4'b1111), .in1(decoder_1_out0), .out(multiplexer_10_out), .sel(id_ex_1_sb_2));
  not not_4 (run, register_2_q);
  EX_MEM ex_mem_1 (
    .I_PC(EX_PC), .I_IR({id_ex_1_o_ir, adder_2_out_2[27:2]}), .RegWrite(EX_RegWrite),
    .MemtoReg(id_ex_1_memtoreg_2), .MemWrite(id_ex_1_memwrite_2), .sel(multiplexer_10_out), .O_PC(MEM_PC),
    .O_IR(ex_mem_1_o_ir), .RegWrite_2(MEM_RegWrite), .MemtoReg_2(ex_mem_1_memtoreg_2),
    .MemWrite_2(ex_mem_1_memwrite_2), .sel_2(ex_mem_1_sel_2), .bubble(1'b0), .en(EN2), .clk(CLK), .clr(RST),
    .W_num(EX_RegWrite_num), .W_num_2(MEM_RegWrite_num), .mem_din(multiplexer_9_out),
    .mem_din_2(ex_mem_1_mem_din_2), .JAL(id_ex_1_jal_2), .JAL_2(ex_mem_1_jal_2), .Halt(and_3_out),
    .Halt_2(ex_mem_1_halt_2), .res1(mips_alu_1_result), .res1_2(ex_mem_1_res1_2));
  Register #(.width(1)) register_2 (.D(1'b1), .en(ex_mem_1_halt_2), .Q(register_2_q), .clk(CLK), .clr(or_7_out));
  or or_7 (or_7_out, RST, Go);
  // MIPS_RAM mips_ram_1: pin names not known; wires that end beside it: ex_mem_1_res1_2[25:2], ex_mem_1_mem_din_2, ex_mem_1_memwrite_2, ex_mem_1_sel_2, CLK, 1'b1, RST, mips_ram_1_p8
  MEM_WB mem_wb_1 (
    .I_PC(MEM_PC), .I_IR(ex_mem_1_o_ir), .RegWrite(MEM_RegWrite), .W_num(MEM_RegWrite_num), .O_PC(WB_PC),
    .RegWrite_2(WB_RegWrite), .W_num_2(mem_wb_1_w_num_2), .bubble(1'b0), .en(EN2), .clk(CLK), .clr(RST),
    .MemOut(mips_ram_1_p8), .MemOut_2(mem_wb_1_memout_2), .res1(ex_mem_1_res1_2), .res1_2(mem_wb_1_res1_2),
    .MemtoReg(ex_mem_1_memtoreg_2), .MemtoReg_2(mem_wb_1_memtoreg_2), .jal(ex_mem_1_jal_2),
    .jal_2(mem_wb_1_jal_2));  // open: O_IR
  Adder #(.width(32)) adder_4 (.a(WB_PC), .b(32'h4), .out(adder_4_out));  // open: cin, cout
  Multiplexer #(.width(32), .enable("false")) multiplexer_11 (
    .in0(mem_wb_1_res1_2), .in1(mem_wb_1_memout_2), .out(multiplexer_11_out), .sel(mem_wb_1_memtoreg_2));
  Multiplexer #(.width(32), .enable("false")) multiplexer_12 (
    .in0(multiplexer_11_out), .in1(adder_4_out), .out(multiplexer_12_out), .sel(mem_wb_1_jal_2));

  // Other names for the same wires on the sheet: EN3 = EN2; EN4 = EN2; ID_R2_num[4:0] = out_1; Func[5:0] = out_2[5:0];
  //   Op[5:0] = out_2[31:26]; PC[31:0] = IF_PC

  // Notes on the sheet:
  //   中断源
  //   中断等待指示
  //   数码管输出
  //   syscall: if $v0(2) == 34 then print $a0(4) else pause
  //   指令存储器
  //   指令字
  //   contents of rom_1 (hex, n*v repeats v):
  //   20110001 8000005 20110001 20120002 20130003 8000009 20110001 20120002 20130003 800000d 20110001
  //   20120002 20130003 8000011 20110001 20120002 20130003 c0000f8 20100001 20110001 118fc0 112020
  //   20020022 c 118882 12200001 8000015 112020 20020022 c 20110001 118880 112020 20020022 c 12200001
  //   800001f 20110001 118fc0 112020 20020022 c 1188c3 112020 20020022 c 118903 112020 20020022 c 118903
  //   112020 20020022 c 118903 112020 20020022 c 118903 112020 20020022 c 118903 112020 20020022 c 118903
  //   112020 20020022 c 118903 112020 20020022 c 20100001 109fc0 139fc3 8021 2012000c 24160003 26100001
  //   3210000f 20080008 20090001 139900 2709825 132020 20020022 c 1094022 1500fff9 22100001 2018000f
  //   2188024 108700 20080008 20090001 139902 2709825 132021 20020022 c 1094022 1500fff9 108702 2c9b022
  //   12c00001 8000050 4020 1084027 84400 3508ffff 82021 20020022 c 2010ffff 20110000 ae300000 22100001
  //   22310004 ae300000 22100001 22310004 ae300000 22100001 22310004 ae300000 22100001 22310004 ae300000
  //   22100001 22310004 ae300000 22100001 22310004 ae300000 22100001 22310004 ae300000 22100001 22310004
  //   ae300000 22100001 22310004 ae300000 22100001 22310004 ae300000 22100001 22310004 ae300000 22100001
  //   22310004 ae300000 22100001 22310004 ae300000 22100001 22310004 ae300000 22100001 22310004 ae300000
  //   22100001 22310004 22100001 8020 2011003c 8e130000 8e340000 274402a 11000002 ae330000 ae140000
  //   2231fffc 1611fff8 102020 20020022 c 22100004 2011003c 1611fff2 20020032 c 20080001 20090003 20110876
  //   118d00 112020 20020022 c 200b0008 1118806 1318806 112020 20020022 c 216bffff 1560fff9 2002000a c
  //   20080001 20110010 112020 20020022 c 200b0020 2288823 112020 20020022 c 216bffff 1560fffa 2002000a c
  //   20090000 200b0020 20110000 20120001 a1310000 112020 20020022 c 2328820 21290001 216bffff 1560fff8
  //   200b0008 20090000 8d310000 112020 20020022 c 21290004 216bffff 1560fff9 2002000a c 2011000f 112020
  //   20020022 c 2231ffff 1e20fffb 2002000a c 2002000a c 20100000 22100001 102020 20020022 c 22100002
  //   102020 20020022 c 22100003 102020 20020022 c 22100004 102020 20020022 c 22100005 102020 20020022 c
  //   22100006 102020 20020022 c 22100007 102020 20020022 c 22100008 102020 20020022 20020022 c 3e00008
  //   OP
  //   Func
  //   rs
  //   rt
  //   rd
  //   流水调试日志用
endmodule

module \重定向流水线  (
  output [31:0] out_1
);

  wire AluSrcB, and_1_out, and_2_out, and_3_out, and_5_out, and_6_out, and_7_out, and_8_out, and_9_out,
       and_10_out, and_11_out, Beq, BGTZ, Bne, bubble1, bubble2, CLK, comparator_1_eq, comparator_2_gt,
       Data_Relate, EN1, EN2, EX_JAL, ex_mem_1_halt_2, ex_mem_1_jal_2, ex_mem_1_memtoreg_2,
       ex_mem_1_memwrite_2, EX_MemtoReg, EX_RegWrite, Go, id_ex_1_alu_src_2, id_ex_1_beq_2, id_ex_1_bgtz_2,
       id_ex_1_bne_2, id_ex_1_jmp_2, id_ex_1_jr_2, id_ex_1_memwrite_2, id_ex_1_sb_2, id_ex_1_shamt_2, IR1,
       IR2, IR3, JAL, JMP, JR, LoadUse, MEM_RegWrite, mem_wb_1_jal_2, mem_wb_1_memtoreg_2, MemToReg,
       MemWrite, mips_alu_1_equal, not_2_out, not_3_out, or_4_out, or_7_out, or_8_out, R1_EX, R1_MEM, R2_EX,
       R2_MEM, RegDst, register_2_q, RegWrite, RST, run, SB, Shamt, SignedExt, Syscall, Syscall_num, W1, W2,
       W3, WB_RegWrite;
  wire [1:0] PCSrc;
  wire [3:0] AluOP, decoder_1_out0, ex_mem_1_sel_2, id_ex_1_alu_op_2, multiplexer_14_out, sel_in;
  wire [4:0] EX_RegWrite_num, ID_R1_num, ID_R2_num, MEM_RegWrite_num, mem_wb_1_w_num_2, multiplexer_2_out,
       multiplexer_3_out, multiplexer_9_out;
  wire [15:0] \LoadUse次数 , \总周期数 , \插入气泡数 , \无条件分支数 , \条件分支成功数 ;
  wire [27:0] adder_2_out;
  wire [31:0] adder_1_out, adder_3_out, adder_4_out, bit_extender_1_out, bit_extender_2_out, EX_ALUres,
       ex_mem_1_mem_din_2, ex_mem_1_o_ir, EX_PC, I_R1, I_R2, id_ex_1_o_imm, ID_PC, IF_PC, LedData,
       MEM_ALUres, MEM_PC, mem_wb_1_memout_2, mem_wb_1_res1_2, mips_ram_1_p8, mips_regifile_1_r1,
       mips_regifile_1_r2, multiplexer_1_out, multiplexer_6_out, multiplexer_7_out, multiplexer_8_out,
       multiplexer_11_out, multiplexer_13_out, multiplexer_15_out, O_R1, O_R2, rom_1_data, shifter_1_out,
       WB_PC, WB_WData;
  wire [31:2] id_ex_1_o_ir;
  wire [31:26] id_ex_1_o_ir_2;

  Button \u_总复位  (.out(RST));
  Button _1 (.out(IR1));
  Button _2 (.out(IR2));
  Button _3 (.out(IR3));
  Button \u_继续运行  (.out(Go));
  LED led_1 (.in(W1));
  LED led_2 (.in(W2));
  LED led_3 (.in(W3));
  not not_1 (EN2, run);
  not not_2 (not_2_out, LoadUse);
  Hex_Digit_Display hex_digit_display_1 (.value(LedData[31:28]));  // open: dp
  and and_1 (and_1_out, LoadUse, run);
  and and_2 (and_2_out, not_2_out, run);
  Register #(.width(32)) PC (.D(multiplexer_1_out), .en(and_2_out), .Q(IF_PC), .clk(CLK), .clr(RST));
  Multiplexer #(.select(2), .width(32), .enable("false")) multiplexer_1 (
    .in0(adder_1_out), .in1(adder_3_out), .in2({id_ex_1_o_ir, 2'b00}), .in3(O_R1), .out(multiplexer_1_out),
    .sel(PCSrc));
  Hex_Digit_Display hex_digit_display_2 (.value(LedData[27:24]));  // open: dp
  Hex_Digit_Display hex_digit_display_3 (.value(LedData[23:20]));  // open: dp
  or or_1 (EN1, LoadUse, EN2);
  or or_2 (bubble1, PCSrc[1], PCSrc[0]);
  Counter #(.width(16), .max('hffff)) counter_1 (
    .count(and_1_out), .Q(\插入气泡数 ), .clk(CLK), .clr(RST));  // open: load, D, carry
  Hex_Digit_Display hex_digit_display_4 (.value(LedData[15:12]));  // open: dp
  Hex_Digit_Display hex_digit_display_5 (.value(LedData[19:16]));  // open: dp
  or or_3 (bubble2, bubble1, LoadUse);
  Counter #(.width(16), .max('hffff)) counter_2 (
    .count(run), .Q(\总周期数 ), .clk(CLK), .clr(RST));  // open: load, D, carry
  Hex_Digit_Display hex_digit_display_6 (.value(LedData[7:4]));  // open: dp
  Hex_Digit_Display hex_digit_display_7 (.value(LedData[11:8]));  // open: dp
  Clock clock_1 (.out(CLK));
  Adder #(.width(32)) adder_1 (.a(IF_PC), .b(32'h4), .out(adder_1_out));  // open: cin, cout
  Hex_Digit_Display hex_digit_display_8 (.value(LedData[3:0]));  // open: dp
  Counter #(.width(16), .max('hffff)) counter_3 (
    .count(and_3_out), .Q(\LoadUse次数 ), .clk(CLK), .clr(RST));  // open: load, D, carry
  and and_3 (and_3_out, LoadUse, run);
  ROM #(.addrWidth(24), .dataWidth(32)) rom_1 (.addr(IF_PC[25:2]), .data(rom_1_data));  // open: sel
  IF_ID if_id_1 (
    .I_PC(IF_PC), .I_IR(rom_1_data), .O_PC(ID_PC), .O_IR(out_1), .bubble(bubble1), .en(EN1), .clk(CLK),
    .clr(RST));  // open: ExpAddr, ExpAddr_2, 预测跳转, 预测跳转_2
  // Probe on \总周期数 
  // Probe on \无条件分支数 
  // Probe on \条件分支成功数 
  // Probe on \插入气泡数 
  // Probe on \LoadUse次数 
  // Probe on IF_PC[11:0]
  Multiplexer #(.width(5), .enable("false")) multiplexer_2 (
    .in0(out_1[20:16]), .in1(out_1[15:11]), .out(multiplexer_2_out), .sel(RegDst));
  Multiplexer #(.width(5), .enable("false")) multiplexer_3 (
    .in0(multiplexer_2_out), .in1({5{1'b1}}), .out(multiplexer_3_out), .sel(JAL));
  assign bit_extender_1_out = {{16{out_1[15]}}, out_1[15:0]};  // Bit_Extender bit_extender_1
  assign bit_extender_2_out = {{16{1'b0}}, out_1[15:0]};  // Bit_Extender bit_extender_2
  // Probe on ID_PC[11:0]
  \数据相关检测扩展  \u_数据相关检测扩展_1  (
    .OP(out_1[31:26]), .EX_WriteReg_num(EX_RegWrite_num), .EX_RegWrite(EX_RegWrite),
    .MEM_WriteReg_num(MEM_RegWrite_num), .MEM_RegWrite(MEM_RegWrite), .\数据相关 (Data_Relate),
    .Func(out_1[5:0]), .ID_R1_num(ID_R1_num), .ID_R2_num(ID_R2_num), .R1_EX(sel_in[0]), .R1_MEM(sel_in[1]),
    .R2_EX(sel_in[2]), .R2_MEM(sel_in[3]));
  Multiplexer #(.width(5), .enable("false")) multiplexer_4 (
    .in0(out_1[25:21]), .in1(5'b00010), .out(ID_R1_num), .sel(Syscall));
  Multiplexer #(.width(5), .enable("false")) multiplexer_5 (
    .in0(out_1[20:16]), .in1(5'b00100), .out(ID_R2_num), .sel(Syscall));
  // Probe on EX_PC[11:0]
  // Probe on MEM_PC[11:0]
  MIPS_Regifile mips_regifile_1 (
    .Din(WB_WData), .Clk(CLK), .R1(mips_regifile_1_r1), .R2(mips_regifile_1_r2), .WE(WB_RegWrite),
    .W_num(mem_wb_1_w_num_2), .R1_num(ID_R1_num), .R2_num(ID_R2_num));
  Multiplexer #(.width(32), .enable("false")) multiplexer_6 (
    .in0(bit_extender_2_out), .in1(bit_extender_1_out), .out(multiplexer_6_out), .sel(SignedExt));
  // Probe on WB_PC[11:0]
  or or_4 (or_4_out, sel_in[0], sel_in[2]);
  ID_EX id_ex_1 (
    .I_PC(ID_PC), .I_IR(out_1), .RegWrite(RegWrite), .MemtoReg(MemToReg), .MemWrite(MemWrite), .SB(SB),
    .ALU_SRC(AluSrcB), .BEQ(Beq), .BNE(Bne), .JR(JR), .JMP(JMP), .JAL(JAL), .BGTZ(BGTZ), .Shamt(Shamt),
    .ALU_OP(AluOP), .syscall(Syscall), .O_PC(EX_PC), .O_IR({id_ex_1_o_ir_2, id_ex_1_o_ir[27:2]}),
    .RegWrite_2(EX_RegWrite), .MemtoReg_2(EX_MemtoReg), .MemWrite_2(id_ex_1_memwrite_2), .SB_2(id_ex_1_sb_2),
    .ALU_SRC_2(id_ex_1_alu_src_2), .BEQ_2(id_ex_1_beq_2), .BNE_2(id_ex_1_bne_2), .JR_2(id_ex_1_jr_2),
    .JMP_2(id_ex_1_jmp_2), .JAL_2(EX_JAL), .BGTZ_2(id_ex_1_bgtz_2), .Shamt_2(id_ex_1_shamt_2),
    .ALU_OP_2(id_ex_1_alu_op_2), .syscall_2(Syscall_num), .bubble(bubble2), .en(EN2), .clk(CLK), .clr(RST),
    .I_R1(mips_regifile_1_r1), .I_R2(mips_regifile_1_r2), .O_R1(I_R1), .O_R2(I_R2),
    .I_Imm(multiplexer_6_out), .O_Imm(id_ex_1_o_imm), .W_num(multiplexer_3_out), .W_num_2(EX_RegWrite_num),
    .sel(sel_in), .sel_2({R2_MEM, R2_EX, R1_MEM, R1_EX}));  // open: ExpAddr, ExpAddr_2, 预测跳转, 预测跳转_2
  Adder #(.width(32)) adder_2 (.a(EX_PC), .b(32'h4), .out({id_ex_1_o_ir[31:28], adder_2_out}));  // open: cin, cout
  \硬布线控制器  \u_硬布线控制器_1  (
    .Func(out_1[5:0]), .OP(out_1[31:26]), .ALU_OP(AluOP), .MemToReg(MemToReg), .MemWrite(MemWrite),
    .ALU_SRC(AluSrcB), .RegWrite(RegWrite), .SysCALL(Syscall), .SignedExt(SignedExt), .RegDst(RegDst),
    .JR(JR), .JMP(JMP), .Beq(Beq), .Bne(Bne), .JAL(JAL), .SHAMT(Shamt), .SB(SB), .BGTZ(BGTZ));
  and and_4 (LoadUse, or_4_out, EX_MemtoReg, ~EX_JAL);  // AND_Gate
  Shifter #(.width(32)) shifter_1 (.in(id_ex_1_o_imm), .\dist (5'b00010), .out(shifter_1_out));
  Adder #(.width(32)) adder_3 (
    .a({id_ex_1_o_ir[31:28], adder_2_out}), .b(shifter_1_out), .out(adder_3_out));  // open: cin, cout
  Comparator #(.width(32)) comparator_1 (.a(32'h22), .b(O_R1), .eq(comparator_1_eq));  // open: gt, lt
  Multiplexer #(.width(32), .disabled(0), .enable("false")) multiplexer_7 (
    .in0(O_R2), .in1(id_ex_1_o_imm), .out(multiplexer_7_out), .sel(id_ex_1_alu_src_2));
  Multiplexer #(.width(32), .enable("false")) multiplexer_8 (
    .in0(I_R1), .in1(WB_WData), .out(multiplexer_8_out), .sel(R1_MEM));
  and and_5 (and_5_out, ~comparator_1_eq, Syscall_num);  // AND_Gate
  and and_6 (and_6_out, comparator_1_eq, Syscall_num);
  Register #(.width(32)) register_1 (.D(O_R2), .en(and_6_out), .Q(LedData), .clk(CLK), .clr(RST));
  MIPS_ALU mips_alu_1 (
    .X(O_R1), .Y(multiplexer_7_out), .AluOP(id_ex_1_alu_op_2), .Equal(mips_alu_1_equal), .Result(EX_ALUres),
    .shamt(multiplexer_9_out));  // open: Result_2
  Multiplexer #(.width(5), .enable("false")) multiplexer_9 (
    .in0(O_R1[4:0]), .in1(id_ex_1_o_ir[12:8]), .out(multiplexer_9_out), .sel(id_ex_1_shamt_2));
  Comparator #(.width(32)) comparator_2 (.a(O_R1), .b({32{1'b0}}), .gt(comparator_2_gt));  // open: eq, lt
  Multiplexer #(.width(32), .enable("false")) multiplexer_10 (
    .in0(multiplexer_8_out), .in1(MEM_ALUres), .out(O_R1), .sel(R1_EX));
  not not_3 (not_3_out, mips_alu_1_equal);
  and and_7 (and_7_out, not_3_out, id_ex_1_bne_2);
  and and_8 (and_8_out, mips_alu_1_equal, id_ex_1_beq_2);
  and and_9 (and_9_out, comparator_2_gt, id_ex_1_bgtz_2);
  Counter #(.width(16), .max('hffff)) counter_4 (
    .count(and_10_out), .Q(\无条件分支数 ), .clk(CLK), .clr(RST));  // open: load, D, carry
  and and_10 (and_10_out, run, PCSrc[1]);
  or or_5 (PCSrc[1], EX_JAL, id_ex_1_jmp_2, id_ex_1_jr_2);
  Multiplexer #(.width(32), .enable("false")) multiplexer_11 (
    .in0(I_R2), .in1(WB_WData), .out(multiplexer_11_out), .sel(R2_MEM));
  or or_6 (PCSrc[0], id_ex_1_jr_2, and_7_out, and_8_out, and_9_out);
  Counter #(.width(16), .max('hffff)) counter_5 (
    .count(and_11_out), .Q(\条件分支成功数 ), .clk(CLK), .clr(RST));  // open: load, D, carry
  and and_11 (and_11_out, run, or_7_out);
  or or_7 (or_7_out, and_7_out, and_8_out, and_9_out);
  Multiplexer #(.width(32), .enable("false")) multiplexer_12 (
    .in0(multiplexer_11_out), .in1(MEM_ALUres), .out(O_R2), .sel(R2_EX));
  Decoder #(.select(2), .enable("false")) decoder_1 (
    .out0(decoder_1_out0[0]), .out1(decoder_1_out0[1]), .out2(decoder_1_out0[2]), .out3(decoder_1_out0[3]),
    .sel(EX_ALUres[1:0]));
  Multiplexer #(.width(32), .enable("false")) multiplexer_13 (
    .in0(O_R2), .in1({O_R2[7:0], O_R2[7:0], O_R2[7:0], O_R2[7:0]}), .out(multiplexer_13_out),
    .sel(id_ex_1_sb_2));
  Multiplexer #(.width(4), .enable("false")) multiplexer_14 (
    .in0(4'b1111), .in1(decoder_1_out0), .out(multiplexer_14_out), .sel(id_ex_1_sb_2));
  not not_4 (run, register_2_q);
  EX_MEM ex_mem_1 (
    .I_PC(EX_PC), .I_IR({id_ex_1_o_ir_2, id_ex_1_o_ir[27:2]}), .RegWrite(EX_RegWrite),
    .MemtoReg(EX_MemtoReg), .MemWrite(id_ex_1_memwrite_2), .sel(multiplexer_14_out), .O_PC(MEM_PC),
    .O_IR(ex_mem_1_o_ir), .RegWrite_2(MEM_RegWrite), .MemtoReg_2(ex_mem_1_memtoreg_2),
    .MemWrite_2(ex_mem_1_memwrite_2), .sel_2(ex_mem_1_sel_2), .bubble(1'b0), .en(EN2), .clk(CLK), .clr(RST),
    .W_num(EX_RegWrite_num), .W_num_2(MEM_RegWrite_num), .mem_din(multiplexer_13_out),
    .mem_din_2(ex_mem_1_mem_din_2), .JAL(EX_JAL), .JAL_2(ex_mem_1_jal_2), .Halt(and_5_out),
    .Halt_2(ex_mem_1_halt_2), .res1(EX_ALUres), .res1_2(MEM_ALUres));
  Register #(.width(1)) register_2 (.D(1'b1), .en(ex_mem_1_halt_2), .Q(register_2_q), .clk(CLK), .clr(or_8_out));
  or or_8 (or_8_out, RST, Go);
  // MIPS_RAM mips_ram_1: pin names not known; wires that end beside it: MEM_ALUres[25:2], ex_mem_1_mem_din_2, ex_mem_1_memwrite_2, ex_mem_1_sel_2, CLK, 1'b1, RST, mips_ram_1_p8
  MEM_WB mem_wb_1 (
    .I_PC(MEM_PC), .I_IR(ex_mem_1_o_ir), .RegWrite(MEM_RegWrite), .W_num(MEM_RegWrite_num), .O_PC(WB_PC),
    .RegWrite_2(WB_RegWrite), .W_num_2(mem_wb_1_w_num_2), .bubble(1'b0), .en(EN2), .clk(CLK), .clr(RST),
    .MemOut(mips_ram_1_p8), .MemOut_2(mem_wb_1_memout_2), .res1(MEM_ALUres), .res1_2(mem_wb_1_res1_2),
    .MemtoReg(ex_mem_1_memtoreg_2), .MemtoReg_2(mem_wb_1_memtoreg_2), .jal(ex_mem_1_jal_2),
    .jal_2(mem_wb_1_jal_2));  // open: O_IR
  Adder #(.width(32)) adder_4 (.a(WB_PC), .b(32'h4), .out(adder_4_out));  // open: cin, cout
  Multiplexer #(.width(32), .enable("false")) multiplexer_15 (
    .in0(mem_wb_1_res1_2), .in1(mem_wb_1_memout_2), .out(multiplexer_15_out), .sel(mem_wb_1_memtoreg_2));
  Multiplexer #(.width(32), .enable("false")) multiplexer_16 (
    .in0(multiplexer_15_out), .in1(adder_4_out), .out(WB_WData), .sel(mem_wb_1_jal_2));

  // Other names for the same wires on the sheet: EN3 = EN2; EN4 = EN2; Func[5:0] = out_1[5:0]; Op[5:0] = out_1[31:26];
  //   PC[31:0] = IF_PC; sel_out[3:0] = {R2_MEM, R2_EX, R1_MEM, R1_EX}

  // Notes on the sheet:
  //   中断源
  //   中断等待指示
  //   数码管输出
  //   syscall: if $v0(2) == 34 then print $a0(4) else pause
  //   指令存储器
  //   指令字
  //   contents of rom_1 (hex, n*v repeats v):
  //   20110001 8000005 20110001 20120002 20130003 8000009 20110001 20120002 20130003 800000d 20110001
  //   20120002 20130003 8000011 20110001 20120002 20130003 c0000f8 20100001 20110001 118fc0 112020
  //   20020022 c 118882 12200001 8000015 112020 20020022 c 20110001 118880 112020 20020022 c 12200001
  //   800001f 20110001 118fc0 112020 20020022 c 1188c3 112020 20020022 c 118903 112020 20020022 c 118903
  //   112020 20020022 c 118903 112020 20020022 c 118903 112020 20020022 c 118903 112020 20020022 c 118903
  //   112020 20020022 c 118903 112020 20020022 c 20100001 109fc0 139fc3 8021 2012000c 24160003 26100001
  //   3210000f 20080008 20090001 139900 2709825 132020 20020022 c 1094022 1500fff9 22100001 2018000f
  //   2188024 108700 20080008 20090001 139902 2709825 132021 20020022 c 1094022 1500fff9 108702 2c9b022
  //   12c00001 8000050 4020 1084027 84400 3508ffff 82021 20020022 c 2010ffff 20110000 ae300000 22100001
  //   22310004 ae300000 22100001 22310004 ae300000 22100001 22310004 ae300000 22100001 22310004 ae300000
  //   22100001 22310004 ae300000 22100001 22310004 ae300000 22100001 22310004 ae300000 22100001 22310004
  //   ae300000 22100001 22310004 ae300000 22100001 22310004 ae300000 22100001 22310004 ae300000 22100001
  //   22310004 ae300000 22100001 22310004 ae300000 22100001 22310004 ae300000 22100001 22310004 ae300000
  //   22100001 22310004 22100001 8020 2011003c 8e130000 8e340000 274402a 11000002 ae330000 ae140000
  //   2231fffc 1611fff8 102020 20020022 c 22100004 2011003c 1611fff2 20020032 c 20080001 20090003 20110876
  //   118d00 112020 20020022 c 200b0008 1118806 1318806 112020 20020022 c 216bffff 1560fff9 2002000a c
  //   20080001 20110010 112020 20020022 c 200b0020 2288823 112020 20020022 c 216bffff 1560fffa 2002000a c
  //   20090000 200b0020 20110000 20120001 a1310000 112020 20020022 c 2328820 21290001 216bffff 1560fff8
  //   200b0008 20090000 8d310000 112020 20020022 c 21290004 216bffff 1560fff9 2002000a c 2011000f 112020
  //   20020022 c 2231ffff 1e20fffb 2002000a c 2002000a c 20100000 22100001 102020 20020022 c 22100002
  //   102020 20020022 c 22100003 102020 20020022 c 22100004 102020 20020022 c 22100005 102020 20020022 c
  //   22100006 102020 20020022 c 22100007 102020 20020022 c 22100008 102020 20020022 20020022 c 3e00008
  //   OP
  //   Func
  //   rs
  //   rt
  //   rd
  //   流水调试日志用
endmodule

module \数据相关检测扩展  (
  input  [5:0] OP,
  input  [4:0] EX_WriteReg_num,
  input  EX_RegWrite,
  input  [4:0] MEM_WriteReg_num,
  input  MEM_RegWrite,
  input  [5:0] Func,
  input  [4:0] ID_R1_num,
  input  [4:0] ID_R2_num,
  output \数据相关 ,
  output R1_EX,
  output R1_MEM,
  output R2_EX,
  output R2_MEM
);

  wire and_1_out, and_2_out, and_3_out, and_4_out, and_6_out, and_8_out, comparator_1_eq, comparator_2_eq,
       comparator_3_eq, comparator_4_eq, comparator_5_eq, comparator_6_eq, or_1_out, or_2_out, R1_Used,
       R2_Used;

  \源寄存器使用情况  \u_源寄存器使用情况_1  (
    .OP0(OP[0]), .OP1(OP[1]), .OP2(OP[2]), .OP3(OP[3]), .OP4(OP[4]), .OP5(OP[5]), .F0(Func[0]), .F1(Func[1]),
    .F2(Func[2]), .F3(Func[3]), .F4(Func[4]), .F5(Func[5]), .R1_Used(R1_Used), .R2_Used(R2_Used));
  Comparator #(.width(5)) comparator_1 (.a(ID_R1_num), .b(EX_WriteReg_num), .eq(comparator_1_eq));  // open: gt, lt
  Comparator #(.width(5)) comparator_2 (.a(ID_R1_num), .b(MEM_WriteReg_num), .eq(comparator_2_eq));  // open: gt, lt
  Comparator #(.width(5)) comparator_3 (.a(ID_R2_num), .b(EX_WriteReg_num), .eq(comparator_3_eq));  // open: gt, lt
  Comparator #(.width(5)) comparator_4 (.a(ID_R2_num), .b(MEM_WriteReg_num), .eq(comparator_4_eq));  // open: gt, lt
  and and_1 (and_1_out, R1_Used, comparator_1_eq, EX_RegWrite);
  and and_2 (and_2_out, R1_Used, comparator_2_eq, MEM_RegWrite);
  and and_3 (and_3_out, R2_Used, comparator_3_eq, EX_RegWrite);
  and and_4 (and_4_out, R2_Used, comparator_4_eq, MEM_RegWrite);
  Comparator #(.width(5)) comparator_5 (.a({5{1'b0}}), .b(ID_R1_num), .eq(comparator_5_eq));  // open: gt, lt
  or or_1 (or_1_out, and_1_out, and_2_out);
  Comparator #(.width(5)) comparator_6 (.a({5{1'b0}}), .b(ID_R2_num), .eq(comparator_6_eq));  // open: gt, lt
  or or_2 (or_2_out, and_3_out, and_4_out);
  and and_5 (R1_EX, ~comparator_5_eq, and_1_out);  // AND_Gate
  and and_6 (and_6_out, ~comparator_5_eq, or_1_out);  // AND_Gate
  and and_7 (R1_MEM, ~comparator_5_eq, and_2_out);  // AND_Gate
  and and_8 (and_8_out, ~comparator_6_eq, or_2_out);  // AND_Gate
  and and_9 (R2_EX, ~comparator_6_eq, and_3_out);  // AND_Gate
  and and_10 (R2_MEM, ~comparator_6_eq, and_4_out);  // AND_Gate
  or or_3 (\数据相关 , and_6_out, and_8_out);

  // Other names for the same wires on the sheet: OP_CODE[5:0] = OP
endmodule
module \动态分支预测  (
  output [31:0] out_1
);

  wire AluSrcB, and_1_out, and_2_out, and_3_out, and_5_out, and_6_out, and_7_out, and_8_out, and_9_out,
       and_10_out, and_11_out, and_12_out, and_13_out, Beq, BGTZ, Bne, bubble1, bubble2, CLK,
       comparator_1_eq, comparator_2_gt, comparator_3_eq, Data_Relate, EN1, EN2, EX_branch, EX_JAL,
       ex_mem_1_halt_2, ex_mem_1_jal_2, ex_mem_1_memtoreg_2, ex_mem_1_memwrite_2, EX_MemtoReg, EX_RegWrite,
       \EX_预测跳转 , Go, id_ex_1_alu_src_2, id_ex_1_beq_2, id_ex_1_bgtz_2, id_ex_1_bne_2, id_ex_1_jmp_2,
       id_ex_1_jr_2, id_ex_1_memwrite_2, id_ex_1_sb_2, id_ex_1_shamt_2, \ID_预测跳转 , IR1, IR2, IR3, JAL, JMP,
       JR, LoadUse, MEM_RegWrite, mem_wb_1_jal_2, mem_wb_1_memtoreg_2, MemToReg, MemWrite, mips_alu_1_equal,
       not_2_out, not_3_out, not_4_out, not_5_out, or_4_out, or_7_out, or_9_out, R1_EX, R1_MEM, R2_EX,
       R2_MEM, RegDst, register_2_q, RegWrite, RST, run, SB, Shamt, SignedExt, Syscall, Syscall_num, W1, W2,
       W3, WB_RegWrite, \预测跳转 ;
  wire [1:0] PCSrc;
  wire [3:0] AluOP, decoder_1_out0, ex_mem_1_sel_2, id_ex_1_alu_op_2, multiplexer_15_out, sel_in;
  wire [4:0] EX_RegWrite_num, ID_R1_num, ID_R2_num, MEM_RegWrite_num, mem_wb_1_w_num_2, multiplexer_3_out,
       multiplexer_4_out, multiplexer_10_out;
  wire [15:0] \LoadUse次数 , \总周期数 , \插入气泡数 , \无条件分支数 , \条件分支成功数 ;
  wire [27:2] id_ex_1_o_ir;
  wire [31:0] adder_3_out, adder_4_out, bit_extender_1_out, bit_extender_2_out, EX_ALUres, EX_ExpAddr,
       ex_mem_1_mem_din_2, ex_mem_1_o_ir, EX_NPC, EX_PC, ExpAddr, I_R1, I_R2, id_ex_1_o_imm, ID_ExpAddr,
       ID_PC, IF_NPC, IF_PC, LedData, MEM_ALUres, MEM_PC, mem_wb_1_memout_2, mem_wb_1_res1_2, mips_ram_1_p8,
       mips_regifile_1_r1, mips_regifile_1_r2, multiplexer_7_out, multiplexer_8_out, multiplexer_9_out,
       multiplexer_12_out, multiplexer_14_out, multiplexer_16_out, multiplexer_18_out, NPCbranch, O_R1, O_R2,
       PCbranch, PCin, rom_1_data, shifter_1_out, WB_PC, WB_WData;
  wire [31:26] id_ex_1_o_ir_2;

  Button \u_总复位  (.out(RST));
  Button _1 (.out(IR1));
  Button _2 (.out(IR2));
  Button _3 (.out(IR3));
  Button \u_继续运行  (.out(Go));
  LED led_1 (.in(W1));
  LED led_2 (.in(W2));
  LED led_3 (.in(W3));
  not not_1 (EN2, run);
  not not_2 (not_2_out, LoadUse);
  Hex_Digit_Display hex_digit_display_1 (.value(LedData[31:28]));  // open: dp
  and and_1 (and_1_out, LoadUse, run);
  and and_2 (and_2_out, not_2_out, run);
  Register #(.width(32)) PC (.D(PCin), .en(and_2_out), .Q(IF_PC), .clk(CLK), .clr(RST));
  Multiplexer #(.select(2), .width(32), .enable("false")) multiplexer_1 (
    .in0(IF_NPC), .in1(adder_3_out), .in2({EX_NPC[31:28], id_ex_1_o_ir, 2'b00}), .in3(O_R1), .out(PCbranch),
    .sel(PCSrc));
  Hex_Digit_Display hex_digit_display_2 (.value(LedData[23:20]));  // open: dp
  Hex_Digit_Display hex_digit_display_3 (.value(LedData[27:24]));  // open: dp
  or or_1 (EN1, LoadUse, EN2);
  or or_2 (EX_branch, PCSrc[1], PCSrc[0]);
  Counter #(.width(16), .max('hffff)) counter_1 (
    .count(and_1_out), .Q(\插入气泡数 ), .clk(CLK), .clr(RST));  // open: load, D, carry
  Multiplexer #(.select(2), .width(32), .enable("false")) multiplexer_2 (
    .in0(EX_NPC), .in1(adder_3_out), .in2({EX_NPC[31:28], id_ex_1_o_ir, 2'b00}), .in3(O_R1), .out(NPCbranch),
    .sel(PCSrc));
  Hex_Digit_Display hex_digit_display_4 (.value(LedData[19:16]));  // open: dp
  Hex_Digit_Display hex_digit_display_5 (.value(LedData[15:12]));  // open: dp
  or or_3 (bubble2, bubble1, LoadUse);
  Counter #(.width(16), .max('hffff)) counter_2 (
    .count(run), .Q(\总周期数 ), .clk(CLK), .clr(RST));  // open: load, D, carry
  Hex_Digit_Display hex_digit_display_6 (.value(LedData[7:4]));  // open: dp
  Hex_Digit_Display hex_digit_display_7 (.value(LedData[11:8]));  // open: dp
  Clock clock_1 (.out(CLK));
  Adder #(.width(32)) adder_1 (.a(IF_PC), .b(32'h4), .out(IF_NPC));  // open: cin, cout
  Hex_Digit_Display hex_digit_display_8 (.value(LedData[3:0]));  // open: dp
  Counter #(.width(16), .max('hffff)) counter_3 (
    .count(and_3_out), .Q(\LoadUse次数 ), .clk(CLK), .clr(RST));  // open: load, D, carry
  and and_3 (and_3_out, LoadUse, run);
  ROM #(.addrWidth(24), .dataWidth(32)) rom_1 (.addr(IF_PC[25:2]), .data(rom_1_data));  // open: sel
  IF_ID if_id_1 (
    .I_PC(IF_PC), .I_IR(rom_1_data), .O_PC(ID_PC), .O_IR(out_1), .bubble(bubble1), .en(EN1), .clk(CLK),
    .clr(RST), .ExpAddr(ExpAddr), .ExpAddr_2(ID_ExpAddr), .\预测跳转 (\预测跳转 ), .\预测跳转_2 (\ID_预测跳转 ));
  // Probe on \总周期数 
  // Probe on \无条件分支数 
  // Probe on \条件分支成功数 
  // Probe on \插入气泡数 
  // Probe on \LoadUse次数 
  // Probe on IF_PC[11:0]
  Multiplexer #(.width(5), .enable("false")) multiplexer_3 (
    .in0(out_1[20:16]), .in1(out_1[15:11]), .out(multiplexer_3_out), .sel(RegDst));
  Multiplexer #(.width(5), .enable("false")) multiplexer_4 (
    .in0(multiplexer_3_out), .in1({5{1'b1}}), .out(multiplexer_4_out), .sel(JAL));
  assign bit_extender_1_out = {{16{out_1[15]}}, out_1[15:0]};  // Bit_Extender bit_extender_1
  assign bit_extender_2_out = {{16{1'b0}}, out_1[15:0]};  // Bit_Extender bit_extender_2
  // Probe on ID_PC[11:0]
  \数据相关检测扩展  \u_数据相关检测扩展_1  (
    .OP(out_1[31:26]), .EX_WriteReg_num(EX_RegWrite_num), .EX_RegWrite(EX_RegWrite),
    .MEM_WriteReg_num(MEM_RegWrite_num), .MEM_RegWrite(MEM_RegWrite), .\数据相关 (Data_Relate),
    .Func(out_1[5:0]), .ID_R1_num(ID_R1_num), .ID_R2_num(ID_R2_num), .R1_EX(sel_in[0]), .R1_MEM(sel_in[1]),
    .R2_EX(sel_in[2]), .R2_MEM(sel_in[3]));
  Multiplexer #(.width(5), .enable("false")) multiplexer_5 (
    .in0(out_1[25:21]), .in1(5'b00010), .out(ID_R1_num), .sel(Syscall));
  Multiplexer #(.width(5), .enable("false")) multiplexer_6 (
    .in0(out_1[20:16]), .in1(5'b00100), .out(ID_R2_num), .sel(Syscall));
  // Probe on MEM_PC[11:0]
  // Probe on EX_PC[11:0]
  MIPS_Regifile mips_regifile_1 (
    .Din(WB_WData), .Clk(CLK), .R1(mips_regifile_1_r1), .R2(mips_regifile_1_r2), .WE(WB_RegWrite),
    .W_num(mem_wb_1_w_num_2), .R1_num(ID_R1_num), .R2_num(ID_R2_num));
  Multiplexer #(.width(32), .enable("false")) multiplexer_7 (
    .in0(bit_extender_2_out), .in1(bit_extender_1_out), .out(multiplexer_7_out), .sel(SignedExt));
  // Probe on WB_PC[11:0]
  or or_4 (or_4_out, sel_in[0], sel_in[2]);
  ID_EX id_ex_1 (
    .I_PC(ID_PC), .I_IR(out_1), .RegWrite(RegWrite), .MemtoReg(MemToReg), .MemWrite(MemWrite), .SB(SB),
    .ALU_SRC(AluSrcB), .BEQ(Beq), .BNE(Bne), .JR(JR), .JMP(JMP), .JAL(JAL), .BGTZ(BGTZ), .Shamt(Shamt),
    .ALU_OP(AluOP), .syscall(Syscall), .O_PC(EX_PC), .O_IR({id_ex_1_o_ir_2, id_ex_1_o_ir}),
    .RegWrite_2(EX_RegWrite), .MemtoReg_2(EX_MemtoReg), .MemWrite_2(id_ex_1_memwrite_2), .SB_2(id_ex_1_sb_2),
    .ALU_SRC_2(id_ex_1_alu_src_2), .BEQ_2(id_ex_1_beq_2), .BNE_2(id_ex_1_bne_2), .JR_2(id_ex_1_jr_2),
    .JMP_2(id_ex_1_jmp_2), .JAL_2(EX_JAL), .BGTZ_2(id_ex_1_bgtz_2), .Shamt_2(id_ex_1_shamt_2),
    .ALU_OP_2(id_ex_1_alu_op_2), .syscall_2(Syscall_num), .bubble(bubble2), .en(EN2), .clk(CLK), .clr(RST),
    .I_R1(mips_regifile_1_r1), .I_R2(mips_regifile_1_r2), .O_R1(I_R1), .O_R2(I_R2),
    .I_Imm(multiplexer_7_out), .O_Imm(id_ex_1_o_imm), .W_num(multiplexer_4_out), .W_num_2(EX_RegWrite_num),
    .sel(sel_in), .sel_2({R2_MEM, R2_EX, R1_MEM, R1_EX}), .ExpAddr(ID_ExpAddr), .ExpAddr_2(EX_ExpAddr),
    .\预测跳转 (\ID_预测跳转 ), .\预测跳转_2 (\EX_预测跳转 ));
  Adder #(.width(32)) adder_2 (.a(EX_PC), .b(32'h4), .out(EX_NPC));  // open: cin, cout
  \硬布线控制器  \u_硬布线控制器_1  (
    .Func(out_1[5:0]), .OP(out_1[31:26]), .ALU_OP(AluOP), .MemToReg(MemToReg), .MemWrite(MemWrite),
    .ALU_SRC(AluSrcB), .RegWrite(RegWrite), .SysCALL(Syscall), .SignedExt(SignedExt), .RegDst(RegDst),
    .JR(JR), .JMP(JMP), .Beq(Beq), .Bne(Bne), .JAL(JAL), .SHAMT(Shamt), .SB(SB), .BGTZ(BGTZ));
  and and_4 (LoadUse, or_4_out, EX_MemtoReg, ~EX_JAL);  // AND_Gate
  Shifter #(.width(32)) shifter_1 (.in(id_ex_1_o_imm), .\dist (5'b00010), .out(shifter_1_out));
  Adder #(.width(32)) adder_3 (.a(EX_NPC), .b(shifter_1_out), .out(adder_3_out));  // open: cin, cout
  // MIPS_Probe mips_probe_1: pin names not known; wires that end beside it: {id_ex_1_o_ir_2, id_ex_1_o_ir}
  Comparator #(.width(32)) comparator_1 (.a(32'h22), .b(O_R1), .eq(comparator_1_eq));  // open: gt, lt
  Multiplexer #(.width(32), .disabled(0), .enable("false")) multiplexer_8 (
    .in0(O_R2), .in1(id_ex_1_o_imm), .out(multiplexer_8_out), .sel(id_ex_1_alu_src_2));
  Multiplexer #(.width(32), .enable("false")) multiplexer_9 (
    .in0(I_R1), .in1(WB_WData), .out(multiplexer_9_out), .sel(R1_MEM));
  and and_5 (and_5_out, ~comparator_1_eq, Syscall_num);  // AND_Gate
  and and_6 (and_6_out, comparator_1_eq, Syscall_num);
  Register #(.width(32)) register_1 (.D(O_R2), .en(and_6_out), .Q(LedData), .clk(CLK), .clr(RST));
  MIPS_ALU mips_alu_1 (
    .X(O_R1), .Y(multiplexer_8_out), .AluOP(id_ex_1_alu_op_2), .Equal(mips_alu_1_equal), .Result(EX_ALUres),
    .shamt(multiplexer_10_out));  // open: Result_2
  Multiplexer #(.width(5), .enable("false")) multiplexer_10 (
    .in0(O_R1[4:0]), .in1(id_ex_1_o_ir[12:8]), .out(multiplexer_10_out), .sel(id_ex_1_shamt_2));
  Comparator #(.width(32)) comparator_2 (.a(O_R1), .b({32{1'b0}}), .gt(comparator_2_gt));  // open: eq, lt
  Multiplexer #(.width(32), .enable("false")) multiplexer_11 (
    .in0(multiplexer_9_out), .in1(MEM_ALUres), .out(O_R1), .sel(R1_EX));
  not not_3 (not_3_out, mips_alu_1_equal);
  and and_7 (and_7_out, not_3_out, id_ex_1_bne_2);
  and and_8 (and_8_out, mips_alu_1_equal, id_ex_1_beq_2);
  and and_9 (and_9_out, comparator_2_gt, id_ex_1_bgtz_2);
  Counter #(.width(16), .max('hffff)) counter_4 (
    .count(and_10_out), .Q(\无条件分支数 ), .clk(CLK), .clr(RST));  // open: load, D, carry
  and and_10 (and_10_out, run, PCSrc[1]);
  or or_5 (PCSrc[1], EX_JAL, id_ex_1_jmp_2, id_ex_1_jr_2);
  Multiplexer #(.width(32), .enable("false")) multiplexer_12 (
    .in0(I_R2), .in1(WB_WData), .out(multiplexer_12_out), .sel(R2_MEM));
  or or_6 (PCSrc[0], id_ex_1_jr_2, and_7_out, and_8_out, and_9_out);
  Counter #(.width(16), .max('hffff)) counter_5 (
    .count(and_11_out), .Q(\条件分支成功数 ), .clk(CLK), .clr(RST));  // open: load, D, carry
  and and_11 (and_11_out, run, or_7_out);
  or or_7 (or_7_out, and_7_out, and_8_out, and_9_out);
  Multiplexer #(.width(32), .enable("false")) multiplexer_13 (
    .in0(multiplexer_12_out), .in1(MEM_ALUres), .out(O_R2), .sel(R2_EX));
  Comparator #(.width(32)) comparator_3 (.a(PCbranch), .b(EX_ExpAddr), .eq(comparator_3_eq));  // open: gt, lt
  not not_4 (not_4_out, comparator_3_eq);
  not not_5 (not_5_out, \EX_预测跳转 );
  BHT bht_1 (
    .EX_Addr(PCbranch), .IF_PC(IF_PC), .EX_PC(EX_PC), .\期望跳转地址 (ExpAddr), .rst(RST), .clk(CLK),
    .EX_branch(EX_branch), .BranchSuc(comparator_3_eq), .\预测跳转 (\预测跳转 ));
  and and_12 (and_12_out, not_4_out, \EX_预测跳转 );
  or or_8 (bubble1, and_12_out, and_13_out);
  and and_13 (and_13_out, not_5_out, EX_branch);
  Decoder #(.select(2), .enable("false")) decoder_1 (
    .out0(decoder_1_out0[0]), .out1(decoder_1_out0[1]), .out2(decoder_1_out0[2]), .out3(decoder_1_out0[3]),
    .sel(EX_ALUres[1:0]));
  Counter #(.width(6), .max('h3f)) counter_6 (.count(\预测跳转 ), .clk(CLK), .clr(RST));  // open: load, D, Q, carry
  Multiplexer #(.width(32), .enable("false")) multiplexer_14 (
    .in0(O_R2), .in1({O_R2[7:0], O_R2[7:0], O_R2[7:0], O_R2[7:0]}), .out(multiplexer_14_out),
    .sel(id_ex_1_sb_2));
  Multiplexer #(.width(4), .enable("false")) multiplexer_15 (
    .in0(4'b1111), .in1(decoder_1_out0), .out(multiplexer_15_out), .sel(id_ex_1_sb_2));
  not not_6 (run, register_2_q);
  EX_MEM ex_mem_1 (
    .I_PC(EX_PC), .I_IR({id_ex_1_o_ir_2, id_ex_1_o_ir}), .RegWrite(EX_RegWrite), .MemtoReg(EX_MemtoReg),
    .MemWrite(id_ex_1_memwrite_2), .sel(multiplexer_15_out), .O_PC(MEM_PC), .O_IR(ex_mem_1_o_ir),
    .RegWrite_2(MEM_RegWrite), .MemtoReg_2(ex_mem_1_memtoreg_2), .MemWrite_2(ex_mem_1_memwrite_2),
    .sel_2(ex_mem_1_sel_2), .bubble(1'b0), .en(EN2), .clk(CLK), .clr(RST), .W_num(EX_RegWrite_num),
    .W_num_2(MEM_RegWrite_num), .mem_din(multiplexer_14_out), .mem_din_2(ex_mem_1_mem_din_2), .JAL(EX_JAL),
    .JAL_2(ex_mem_1_jal_2), .Halt(and_5_out), .Halt_2(ex_mem_1_halt_2), .res1(EX_ALUres), .res1_2(MEM_ALUres));
  Multiplexer #(.width(32), .enable("false")) multiplexer_16 (
    .in0(IF_NPC), .in1(ExpAddr), .out(multiplexer_16_out), .sel(\预测跳转 ));
  Register #(.width(1)) register_2 (.D(1'b1), .en(ex_mem_1_halt_2), .Q(register_2_q), .clk(CLK), .clr(or_9_out));
  Multiplexer #(.width(32), .enable("false")) multiplexer_17 (
    .in0(multiplexer_16_out), .in1(NPCbranch), .out(PCin), .sel(bubble1));
  or or_9 (or_9_out, RST, Go);
  // MIPS_RAM mips_ram_1: pin names not known; wires that end beside it: MEM_ALUres[25:2], ex_mem_1_mem_din_2, ex_mem_1_memwrite_2, ex_mem_1_sel_2, CLK, 1'b1, RST, mips_ram_1_p8
  MEM_WB mem_wb_1 (
    .I_PC(MEM_PC), .I_IR(ex_mem_1_o_ir), .RegWrite(MEM_RegWrite), .W_num(MEM_RegWrite_num), .O_PC(WB_PC),
    .RegWrite_2(WB_RegWrite), .W_num_2(mem_wb_1_w_num_2), .bubble(1'b0), .en(EN2), .clk(CLK), .clr(RST),
    .MemOut(mips_ram_1_p8), .MemOut_2(mem_wb_1_memout_2), .res1(MEM_ALUres), .res1_2(mem_wb_1_res1_2),
    .MemtoReg(ex_mem_1_memtoreg_2), .MemtoReg_2(mem_wb_1_memtoreg_2), .jal(ex_mem_1_jal_2),
    .jal_2(mem_wb_1_jal_2));  // open: O_IR
  Adder #(.width(32)) adder_4 (.a(WB_PC), .b(32'h4), .out(adder_4_out));  // open: cin, cout
  Multiplexer #(.width(32), .enable("false")) multiplexer_18 (
    .in0(mem_wb_1_res1_2), .in1(mem_wb_1_memout_2), .out(multiplexer_18_out), .sel(mem_wb_1_memtoreg_2));
  Multiplexer #(.width(32), .enable("false")) multiplexer_19 (
    .in0(multiplexer_18_out), .in1(adder_4_out), .out(WB_WData), .sel(mem_wb_1_jal_2));

  // Other names for the same wires on the sheet: EN3 = EN2; EN4 = EN2; fault = bubble1; Func[5:0] = out_1[5:0];
  //   Op[5:0] = out_1[31:26]; PC[31:0] = IF_PC; sel_out[3:0] = {R2_MEM, R2_EX, R1_MEM, R1_EX}

  // Notes on the sheet:
  //   中断源
  //   中断等待指示
  //   数码管输出
  //   syscall: if $v0(2) == 34 then print $a0(4) else pause
  //   指令存储器
  //   指令字
  //   contents of rom_1 (hex, n*v repeats v):
  //   20110001 8000005 20110001 20120002 20130003 8000009 20110001 20120002 20130003 800000d 20110001
  //   20120002 20130003 8000011 20110001 20120002 20130003 c0000f8 20100001 20110001 118fc0 112020
  //   20020022 c 118882 12200001 8000015 112020 20020022 c 20110001 118880 112020 20020022 c 12200001
  //   800001f 20110001 118fc0 112020 20020022 c 1188c3 112020 20020022 c 118903 112020 20020022 c 118903
  //   112020 20020022 c 118903 112020 20020022 c 118903 112020 20020022 c 118903 112020 20020022 c 118903
  //   112020 20020022 c 118903 112020 20020022 c 20100001 109fc0 139fc3 8021 2012000c 24160003 26100001
  //   3210000f 20080008 20090001 139900 2709825 132020 20020022 c 1094022 1500fff9 22100001 2018000f
  //   2188024 108700 20080008 20090001 139902 2709825 132021 20020022 c 1094022 1500fff9 108702 2c9b022
  //   12c00001 8000050 4020 1084027 84400 3508ffff 82021 20020022 c 2010ffff 20110000 ae300000 22100001
  //   22310004 ae300000 22100001 22310004 ae300000 22100001 22310004 ae300000 22100001 22310004 ae300000
  //   22100001 22310004 ae300000 22100001 22310004 ae300000 22100001 22310004 ae300000 22100001 22310004
  //   ae300000 22100001 22310004 ae300000 22100001 22310004 ae300000 22100001 22310004 ae300000 22100001
  //   22310004 ae300000 22100001 22310004 ae300000 22100001 22310004 ae300000 22100001 22310004 ae300000
  //   22100001 22310004 22100001 8020 2011003c 8e130000 8e340000 274402a 11000002 ae330000 ae140000
  //   2231fffc 1611fff8 102020 20020022 c 22100004 2011003c 1611fff2 20020032 c 20080001 20090003 20110876
  //   118d00 112020 20020022 c 200b0008 1118806 1318806 112020 20020022 c 216bffff 1560fff9 2002000a c
  //   20080001 20110010 112020 20020022 c 200b0020 2288823 112020 20020022 c 216bffff 1560fffa 2002000a c
  //   20090000 200b0020 20110000 20120001 a1310000 112020 20020022 c 2328820 21290001 216bffff 1560fff8
  //   200b0008 20090000 8d310000 112020 20020022 c 21290004 216bffff 1560fff9 2002000a c 2011000f 112020
  //   20020022 c 2231ffff 1e20fffb 2002000a c 2002000a c 20100000 22100001 102020 20020022 c 22100002
  //   102020 20020022 c 22100003 102020 20020022 c 22100004 102020 20020022 c 22100005 102020 20020022 c
  //   22100006 102020 20020022 c 22100007 102020 20020022 c 22100008 102020 20020022 20020022 c 3e00008
  //   OP
  //   Func
  //   rs
  //   rt
  //   rd
  //   流水调试日志用
endmodule

module \状态机转移逻辑  (
  input  BranchSuc,
  input  [1:0] state,
  output [1:0] next_state
);

  wire and_1_out, and_2_out, and_3_out, and_4_out, not_1_out, not_2_out, not_3_out, not_4_out, not_5_out;

  not not_1 (not_1_out, state[0]);
  not not_2 (not_2_out, BranchSuc);
  not not_3 (not_3_out, state[0]);
  not not_4 (not_4_out, state[1]);
  not not_5 (not_5_out, state[0]);
  and and_1 (and_1_out, state[1], not_1_out);
  and and_2 (and_2_out, BranchSuc, state[0]);
  and and_3 (and_3_out, not_2_out, state[1], not_3_out);
  and and_4 (and_4_out, BranchSuc, not_4_out, not_5_out);
  or or_1 (next_state[1], and_1_out, and_2_out);
  or or_2 (next_state[0], and_3_out, and_4_out);
endmodule

module BHT (
  input  [31:0] EX_Addr,
  input  [31:0] IF_PC,
  input  [31:0] EX_PC,
  input  rst,
  input  clk,
  input  EX_branch,
  input  BranchSuc,
  output [31:0] \期望跳转地址 ,
  output \预测跳转 
);

  wire and_1_out, comparator_2_eq, comparator_3_eq, comparator_4_eq, comparator_5_eq, comparator_6_eq,
       comparator_7_eq, comparator_8_eq, comparator_9_eq, comparator_10_eq, comparator_11_eq,
       comparator_12_eq, comparator_13_eq, comparator_14_eq, comparator_15_eq, comparator_16_eq,
       comparator_17_eq, HitR, HitW, L0, L1, L2, L3, L4, L5, L6, L7, MissR, MissW, not_1_out, not_2_out,
       not_3_out, not_4_out, not_5_out, not_6_out, not_7_out, not_8_out, not_9_out, not_10_out, not_11_out,
       not_12_out, not_13_out, not_14_out, not_15_out, not_16_out, or_1_out, or_2_out, or_3_out, or_4_out,
       or_5_out, or_6_out, or_7_out, or_8_out, or_9_out, or_10_out, or_11_out, or_12_out, or_13_out,
       or_14_out, or_15_out, or_16_out, priority_encoder_1_en_out, R0, R1, R2, R3, R4, R5, R6, R7, sel0,
       sel1, sel2, sel3, sel4, sel5, sel6, sel7, V0, V1, V2, V3, V4, V5, V6, V7;
  wire [1:0] multiplexer_1_out, multiplexer_2_out, multiplexer_3_out, multiplexer_4_out, multiplexer_5_out,
       multiplexer_6_out, multiplexer_7_out, multiplexer_8_out, register_25_q, register_26_q, register_27_q,
       register_28_q, register_29_q, register_30_q, register_31_q, register_32_q, StateOut,
       \状态机转移逻辑_1_next_state , \状态机转移逻辑_2_next_state , \状态机转移逻辑_3_next_state , \状态机转移逻辑_4_next_state ,
       \状态机转移逻辑_5_next_state , \状态机转移逻辑_6_next_state , \状态机转移逻辑_7_next_state , \状态机转移逻辑_8_next_state ;
  wire [2:0] max3_1_max_num, max3_2_max_num, max3_3_max_num, max3_4_max_num, max3_5_max_num, max3_6_max_num,
       max3_7_max_num, multiplexer_9_out, priority_encoder_1_out;
  wire [15:0] C0, C1, C2, C3, C4, C5, C6, C7, max3_2_max, max3_3_max, max3_4_max, max3_5_max, max3_6_max,
       max3_7_max;
  wire [31:0] PC0, PC1, PC2, PC3, PC4, PC5, PC6, PC7, register_17_q, register_18_q, register_19_q,
       register_20_q, register_21_q, register_22_q, register_23_q, register_24_q;

  Register #(.width(1)) register_1 (.D(1'b1), .en(sel0), .Q(V0), .clk(clk), .clr(rst));
  Register #(.width(1)) register_2 (.D(1'b1), .en(sel1), .Q(V1), .clk(clk), .clr(rst));
  Register #(.width(1)) register_3 (.D(1'b1), .en(sel2), .Q(V2), .clk(clk), .clr(rst));
  Register #(.width(1)) register_4 (.D(1'b1), .en(sel3), .Q(V3), .clk(clk), .clr(rst));
  Register #(.width(1)) register_5 (.D(1'b1), .en(sel4), .Q(V4), .clk(clk), .clr(rst));
  Register #(.width(1)) register_6 (.D(1'b1), .en(sel5), .Q(V5), .clk(clk), .clr(rst));
  Register #(.width(1)) register_7 (.D(1'b1), .en(sel6), .Q(V6), .clk(clk), .clr(rst));
  Register #(.width(1)) register_8 (.D(1'b1), .en(sel7), .Q(V7), .clk(clk), .clr(rst));
  Register #(.width(32)) register_9 (.D(EX_PC), .en(sel0), .Q(PC0), .clk(clk), .clr(rst));
  or or_1 (or_1_out, sel0, R0);
  Register #(.width(32)) register_10 (.D(EX_PC), .en(sel1), .Q(PC1), .clk(clk), .clr(rst));
  or or_2 (or_2_out, sel1, R1);
  Register #(.width(32)) register_11 (.D(EX_PC), .en(sel2), .Q(PC2), .clk(clk), .clr(rst));
  or or_3 (or_3_out, sel2, R2);
  Register #(.width(32)) register_12 (.D(EX_PC), .en(sel3), .Q(PC3), .clk(clk), .clr(rst));
  or or_4 (or_4_out, sel3, R3);
  Register #(.width(32)) register_13 (.D(EX_PC), .en(sel4), .Q(PC4), .clk(clk), .clr(rst));
  or or_5 (or_5_out, sel4, R4);
  Register #(.width(32)) register_14 (.D(EX_PC), .en(sel5), .Q(PC5), .clk(clk), .clr(rst));
  or or_6 (or_6_out, sel5, R5);
  Register #(.width(32)) register_15 (.D(EX_PC), .en(sel6), .Q(PC6), .clk(clk), .clr(rst));
  or or_7 (or_7_out, sel6, R6);
  Register #(.width(32)) register_16 (.D(EX_PC), .en(sel7), .Q(PC7), .clk(clk), .clr(rst));
  or or_8 (or_8_out, sel7, R7);
  not not_1 (not_1_out, or_1_out);
  not not_2 (not_2_out, or_2_out);
  not not_3 (not_3_out, or_3_out);
  not not_4 (not_4_out, or_4_out);
  not not_5 (not_5_out, or_5_out);
  not not_6 (not_6_out, or_6_out);
  not not_7 (not_7_out, or_7_out);
  Counter #(.width(16), .max('hffff)) counter_1 (
    .load(or_1_out), .D({16{1'b0}}), .count(not_1_out), .Q(C0), .clk(clk), .clr(rst));  // open: carry
  Counter #(.width(16), .max('hffff)) counter_2 (
    .load(or_2_out), .D({16{1'b0}}), .count(not_2_out), .Q(C1), .clk(clk), .clr(rst));  // open: carry
  Counter #(.width(16), .max('hffff)) counter_3 (
    .load(or_3_out), .D({16{1'b0}}), .count(not_3_out), .Q(C2), .clk(clk), .clr(rst));  // open: carry
  Counter #(.width(16), .max('hffff)) counter_4 (
    .load(or_4_out), .D({16{1'b0}}), .count(not_4_out), .Q(C3), .clk(clk), .clr(rst));  // open: carry
  Counter #(.width(16), .max('hffff)) counter_5 (
    .load(or_5_out), .D({16{1'b0}}), .count(not_5_out), .Q(C4), .clk(clk), .clr(rst));  // open: carry
  Counter #(.width(16), .max('hffff)) counter_6 (
    .load(or_6_out), .D({16{1'b0}}), .count(not_6_out), .Q(C5), .clk(clk), .clr(rst));  // open: carry
  Counter #(.width(16), .max('hffff)) counter_7 (
    .load(or_7_out), .D({16{1'b0}}), .count(not_7_out), .Q(C6), .clk(clk), .clr(rst));  // open: carry
  Counter #(.width(16), .max('hffff)) counter_8 (
    .load(or_8_out), .D({16{1'b0}}), .count(not_8_out), .Q(C7), .clk(clk), .clr(rst));  // open: carry
  not not_8 (not_8_out, or_8_out);
  Register #(.width(32)) register_17 (.D(EX_Addr), .en(sel0), .Q(register_17_q), .clk(clk), .clr(rst));
  Register #(.width(32)) register_18 (.D(EX_Addr), .en(sel1), .Q(register_18_q), .clk(clk), .clr(rst));
  Register #(.width(32)) register_19 (.D(EX_Addr), .en(sel2), .Q(register_19_q), .clk(clk), .clr(rst));
  Register #(.width(32)) register_20 (.D(EX_Addr), .en(sel3), .Q(register_20_q), .clk(clk), .clr(rst));
  Register #(.width(32)) register_21 (.D(EX_Addr), .en(sel4), .Q(register_21_q), .clk(clk), .clr(rst));
  Register #(.width(32)) register_22 (.D(EX_Addr), .en(sel5), .Q(register_22_q), .clk(clk), .clr(rst));
  Register #(.width(32)) register_23 (.D(EX_Addr), .en(sel6), .Q(register_23_q), .clk(clk), .clr(rst));
  Register #(.width(32)) register_24 (.D(EX_Addr), .en(sel7), .Q(register_24_q), .clk(clk), .clr(rst));
  assign \期望跳转地址  = L0 ? register_17_q : 32'bz;  // Controlled_Buffer controlled_buffer_1
  assign \期望跳转地址  = L1 ? register_18_q : 32'bz;  // Controlled_Buffer controlled_buffer_2
  assign \期望跳转地址  = L2 ? register_19_q : 32'bz;  // Controlled_Buffer controlled_buffer_3
  assign \期望跳转地址  = L3 ? register_20_q : 32'bz;  // Controlled_Buffer controlled_buffer_4
  assign \期望跳转地址  = L4 ? register_21_q : 32'bz;  // Controlled_Buffer controlled_buffer_5
  assign \期望跳转地址  = L5 ? register_22_q : 32'bz;  // Controlled_Buffer controlled_buffer_6
  assign \期望跳转地址  = L6 ? register_23_q : 32'bz;  // Controlled_Buffer controlled_buffer_7
  assign \期望跳转地址  = L7 ? register_24_q : 32'bz;  // Controlled_Buffer controlled_buffer_8
  Pull_Resistor pull_resistor_1 (.node(\期望跳转地址 ));
  \状态机转移逻辑  \u_状态机转移逻辑_1  (.BranchSuc(BranchSuc), .state(register_26_q), .next_state(\状态机转移逻辑_1_next_state ));
  \状态机转移逻辑  \u_状态机转移逻辑_2  (.BranchSuc(BranchSuc), .state(register_27_q), .next_state(\状态机转移逻辑_2_next_state ));
  \状态机转移逻辑  \u_状态机转移逻辑_3  (.BranchSuc(BranchSuc), .state(register_28_q), .next_state(\状态机转移逻辑_3_next_state ));
  \状态机转移逻辑  \u_状态机转移逻辑_4  (.BranchSuc(BranchSuc), .state(register_29_q), .next_state(\状态机转移逻辑_4_next_state ));
  \状态机转移逻辑  \u_状态机转移逻辑_5  (.BranchSuc(BranchSuc), .state(register_30_q), .next_state(\状态机转移逻辑_5_next_state ));
  \状态机转移逻辑  \u_状态机转移逻辑_6  (.BranchSuc(BranchSuc), .state(register_31_q), .next_state(\状态机转移逻辑_6_next_state ));
  \状态机转移逻辑  \u_状态机转移逻辑_7  (.BranchSuc(BranchSuc), .state(register_32_q), .next_state(\状态机转移逻辑_7_next_state ));
  or or_9 (or_9_out, sel5, R5);
  \状态机转移逻辑  \u_状态机转移逻辑_8  (.BranchSuc(BranchSuc), .state(register_25_q), .next_state(\状态机转移逻辑_8_next_state ));
  or or_10 (or_10_out, sel6, R6);
  Multiplexer #(.width(2), .enable("false")) multiplexer_1 (
    .in0(\状态机转移逻辑_1_next_state ), .in1(2'b00), .out(multiplexer_1_out), .sel(sel6));
  or or_11 (or_11_out, sel7, R7);
  Multiplexer #(.width(2), .enable("false")) multiplexer_2 (
    .in0(\状态机转移逻辑_2_next_state ), .in1(2'b00), .out(multiplexer_2_out), .sel(sel7));
  or or_12 (or_12_out, sel0, R0);
  Multiplexer #(.width(2), .enable("false")) multiplexer_3 (
    .in0(\状态机转移逻辑_3_next_state ), .in1(2'b00), .out(multiplexer_3_out), .sel(sel0));
  or or_13 (or_13_out, sel1, R1);
  Multiplexer #(.width(2), .enable("false")) multiplexer_4 (
    .in0(\状态机转移逻辑_4_next_state ), .in1(2'b00), .out(multiplexer_4_out), .sel(sel1));
  or or_14 (or_14_out, sel2, R2);
  Multiplexer #(.width(2), .enable("false")) multiplexer_5 (
    .in0(\状态机转移逻辑_5_next_state ), .in1(2'b00), .out(multiplexer_5_out), .sel(sel2));
  or or_15 (or_15_out, sel3, R3);
  Multiplexer #(.width(2), .enable("false")) multiplexer_6 (
    .in0(\状态机转移逻辑_6_next_state ), .in1(2'b00), .out(multiplexer_6_out), .sel(sel3));
  or or_16 (or_16_out, sel4, R4);
  Multiplexer #(.width(2), .enable("false")) multiplexer_7 (
    .in0(\状态机转移逻辑_7_next_state ), .in1(2'b00), .out(multiplexer_7_out), .sel(sel4));
  Register #(.width(2)) register_25 (.D(multiplexer_8_out), .en(or_9_out), .Q(register_25_q), .clk(clk), .clr(rst));
  Multiplexer #(.width(2), .enable("false")) multiplexer_8 (
    .in0(\状态机转移逻辑_8_next_state ), .in1(2'b00), .out(multiplexer_8_out), .sel(sel5));
  Register #(.width(2)) register_26 (.D(multiplexer_1_out), .en(or_10_out), .Q(register_26_q), .clk(clk), .clr(rst));
  Register #(.width(2)) register_27 (.D(multiplexer_2_out), .en(or_11_out), .Q(register_27_q), .clk(clk), .clr(rst));
  Register #(.width(2)) register_28 (.D(multiplexer_3_out), .en(or_12_out), .Q(register_28_q), .clk(clk), .clr(rst));
  Register #(.width(2)) register_29 (.D(multiplexer_4_out), .en(or_13_out), .Q(register_29_q), .clk(clk), .clr(rst));
  Register #(.width(2)) register_30 (.D(multiplexer_5_out), .en(or_14_out), .Q(register_30_q), .clk(clk), .clr(rst));
  Register #(.width(2)) register_31 (.D(multiplexer_6_out), .en(or_15_out), .Q(register_31_q), .clk(clk), .clr(rst));
  Register #(.width(2)) register_32 (.D(multiplexer_7_out), .en(or_16_out), .Q(register_32_q), .clk(clk), .clr(rst));
  assign StateOut = L6 ? register_26_q : 2'bz;  // Controlled_Buffer controlled_buffer_9
  assign StateOut = L7 ? register_27_q : 2'bz;  // Controlled_Buffer controlled_buffer_10
  Pull_Resistor pull_resistor_2 (.node(StateOut));
  assign StateOut = L0 ? register_28_q : 2'bz;  // Controlled_Buffer controlled_buffer_11
  assign StateOut = L1 ? register_29_q : 2'bz;  // Controlled_Buffer controlled_buffer_12
  assign StateOut = L2 ? register_30_q : 2'bz;  // Controlled_Buffer controlled_buffer_13
  assign StateOut = L3 ? register_31_q : 2'bz;  // Controlled_Buffer controlled_buffer_14
  assign StateOut = L4 ? register_32_q : 2'bz;  // Controlled_Buffer controlled_buffer_15
  assign StateOut = L5 ? register_25_q : 2'bz;  // Controlled_Buffer controlled_buffer_16
  Comparator #(.width(2), .mode("unsigned")) comparator_1 (.a(StateOut), .b(2'b01), .gt(\预测跳转 ));  // open: eq, lt
  Comparator #(.width(32)) comparator_2 (.a(EX_PC), .b(PC0), .eq(comparator_2_eq));  // open: gt, lt
  Comparator #(.width(32)) comparator_3 (.a(EX_PC), .b(PC1), .eq(comparator_3_eq));  // open: gt, lt
  Comparator #(.width(32)) comparator_4 (.a(EX_PC), .b(PC2), .eq(comparator_4_eq));  // open: gt, lt
  Comparator #(.width(32)) comparator_5 (.a(EX_PC), .b(PC3), .eq(comparator_5_eq));  // open: gt, lt
  Comparator #(.width(32)) comparator_6 (.a(EX_PC), .b(PC4), .eq(comparator_6_eq));  // open: gt, lt
  Comparator #(.width(32)) comparator_7 (.a(EX_PC), .b(PC5), .eq(comparator_7_eq));  // open: gt, lt
  Comparator #(.width(32)) comparator_8 (.a(EX_PC), .b(PC6), .eq(comparator_8_eq));  // open: gt, lt
  Comparator #(.width(32)) comparator_9 (.a(EX_PC), .b(PC7), .eq(comparator_9_eq));  // open: gt, lt
  not not_9 (not_9_out, V0);
  not not_10 (not_10_out, V1);
  not not_11 (not_11_out, V2);
  not not_12 (not_12_out, V3);
  not not_13 (not_13_out, V4);
  not not_14 (not_14_out, V5);
  not not_15 (not_15_out, V6);
  not not_16 (not_16_out, V7);
  Comparator #(.width(32)) comparator_10 (.a(IF_PC), .b(PC0), .eq(comparator_10_eq));  // open: gt, lt
  Comparator #(.width(32)) comparator_11 (.a(IF_PC), .b(PC1), .eq(comparator_11_eq));  // open: gt, lt
  Comparator #(.width(32)) comparator_12 (.a(IF_PC), .b(PC2), .eq(comparator_12_eq));  // open: gt, lt
  Comparator #(.width(32)) comparator_13 (.a(IF_PC), .b(PC3), .eq(comparator_13_eq));  // open: gt, lt
  Comparator #(.width(32)) comparator_14 (.a(IF_PC), .b(PC4), .eq(comparator_14_eq));  // open: gt, lt
  Comparator #(.width(32)) comparator_15 (.a(IF_PC), .b(PC5), .eq(comparator_15_eq));  // open: gt, lt
  Comparator #(.width(32)) comparator_16 (.a(IF_PC), .b(PC6), .eq(comparator_16_eq));  // open: gt, lt
  Comparator #(.width(32)) comparator_17 (.a(IF_PC), .b(PC7), .eq(comparator_17_eq));  // open: gt, lt
  and and_1 (and_1_out, MissW, EX_branch);
  Priority_Encoder priority_encoder_1 (
    .in0(not_9_out), .in1(not_10_out), .in2(not_11_out), .in3(not_12_out), .in4(not_13_out),
    .in5(not_14_out), .in6(not_15_out), .in7(not_16_out), .out(priority_encoder_1_out),
    .en_out(priority_encoder_1_en_out));  // open: en_in, gs
  and and_2 (R0, comparator_2_eq, V0);
  and and_3 (R1, comparator_3_eq, V1);
  and and_4 (R2, comparator_4_eq, V2);
  and and_5 (R3, comparator_5_eq, V3);
  and and_6 (R4, comparator_6_eq, V4);
  and and_7 (R5, comparator_7_eq, V5);
  and and_8 (R6, comparator_8_eq, V6);
  and and_9 (R7, comparator_9_eq, V7);
  and and_10 (L0, V0, comparator_10_eq);
  and and_11 (L1, V1, comparator_11_eq);
  and and_12 (L2, V2, comparator_12_eq);
  and and_13 (L3, V3, comparator_13_eq);
  and and_14 (L4, V4, comparator_14_eq);
  and and_15 (L5, V5, comparator_15_eq);
  and and_16 (L6, V6, comparator_16_eq);
  and and_17 (L7, V7, comparator_17_eq);
  Decoder #(.select(3), .disabled(0)) decoder_1 (
    .out0(sel0), .out1(sel1), .out2(sel2), .out3(sel3), .out4(sel4), .out5(sel5), .out6(sel6), .out7(sel7),
    .sel(multiplexer_9_out), .en(and_1_out));
  Multiplexer #(.width(3), .enable("false")) multiplexer_9 (
    .in0(priority_encoder_1_out), .in1(max3_1_max_num), .out(multiplexer_9_out),
    .sel(priority_encoder_1_en_out));
  or or_17 (HitW, R0, R1, R2, R3, R4, R5, R6, R7);
  MAX3 max3_1 (
    .Y(max3_2_max), .X(max3_3_max), .Y_num(max3_2_max_num), .X_num(max3_3_max_num), .Max_num(max3_1_max_num));  // open: MAX
  not not_17 (MissW, HitW);
  MAX3 max3_2 (
    .Y(max3_7_max), .X(max3_6_max), .Y_num(max3_7_max_num), .X_num(max3_6_max_num), .MAX(max3_2_max),
    .Max_num(max3_2_max_num));
  MAX3 max3_3 (
    .Y(max3_5_max), .X(max3_4_max), .Y_num(max3_5_max_num), .X_num(max3_4_max_num), .MAX(max3_3_max),
    .Max_num(max3_3_max_num));
  or or_18 (HitR, L0, L1, L2, L3, L4, L5, L6, L7);
  MAX3 max3_4 (.Y(C1), .X(C0), .Y_num(3'b001), .X_num(3'b000), .MAX(max3_4_max), .Max_num(max3_4_max_num));
  MAX3 max3_5 (.Y(C3), .X(C2), .Y_num(3'b011), .X_num(3'b010), .MAX(max3_5_max), .Max_num(max3_5_max_num));
  MAX3 max3_6 (.Y(C5), .X(C4), .Y_num(3'b101), .X_num(3'b100), .MAX(max3_6_max), .Max_num(max3_6_max_num));
  MAX3 max3_7 (.Y(C7), .X(C6), .Y_num(3'b111), .X_num(3'b110), .MAX(max3_7_max), .Max_num(max3_7_max_num));
  not not_18 (MissR, HitR);

  // Other names for the same wires on the sheet: branch = EX_branch; slotD[31:0] = \期望跳转地址 ; 跳转地址[31:0] = \期望跳转地址 

  // Notes on the sheet:
  //   输入引脚区
  //   输出引脚区
endmodule

module MAX3 (
  input  [15:0] Y,
  input  [15:0] X,
  input  [2:0] Y_num,
  input  [2:0] X_num,
  output [15:0] MAX,
  output [2:0] Max_num
);

  wire comparator_1_gt;

  Multiplexer #(.width(16), .enable("false")) multiplexer_1 (.in0(Y), .in1(X), .out(MAX), .sel(comparator_1_gt));
  Comparator #(.width(16), .mode("unsigned")) comparator_1 (.a(X), .b(Y), .gt(comparator_1_gt));  // open: eq, lt
  Multiplexer #(.width(3), .enable("false")) multiplexer_2 (
    .in0(Y_num), .in1(X_num), .out(Max_num), .sel(comparator_1_gt));

  // Notes on the sheet:
  //   输出两个输入中的较大值，并输出较大值的3位编号
endmodule

module \多级中断单周期  (
  output [31:0] out_1,
  output [1:0] out_2,
  output [3:0] out_3,
  output [4:0] out_4
);

  wire AluSrcB, and_1_out, and_2_out, and_3_out, and_6_out, and_9_out, and_11_out, and_12_out, and_13_out,
       and_14_out, and_15_out, and_16_out, backupPC, Beq, BGTZ, bit_extender_1_out, Bne, CLK,
       comparator_1_eq, comparator_2_eq, comparator_3_eq, comparator_4_eq, comparator_5_gt, d_ff_1_q,
       d_ff_2_q, d_ff_3_q, EPC_Write, ERET, Go, IE_Write, INM_write, INT1_CLR, INT2_CLR, INT3_CLR, INT_CLI,
       INT_FLG, INT_SIG, \INT脉冲 , IR1, IR2, IR3, JAL, JMP, JR, MemToReg, MemWrite, MFC0, mips_alu_1_equal,
       MTC0, multiplexer_2_out, multiplexer_14_out, multiplexer_18_out, not_1_out, not_2_out, or_4_out,
       or_5_out, or_6_out, or_7_out, or_8_out, or_9_out, or_10_out, or_11_out, or_12_out, or_13_out,
       or_16_out, or_17_out, RegDst, register_1_q, register_2_q, register_6_q, RegWrite, RST, SB, Shamt,
       SignedExt, Syscall, W1, W2, W3, xnor_1_out;
  wire [1:0] priority_encoder_1_out, register_3_q;
  wire [2:0] and_5_out, d_ff_4_q;
  wire [3:0] decoder_2_out0, multiplexer_17_out;
  wire [4:0] mips_regifile_1_r1, multiplexer_6_out, multiplexer_8_out, multiplexer_9_out, multiplexer_13_out,
       rd;
  wire [5:0] Func, Op;
  wire [7:0] mips_regifile_1_r2_2;
  wire [15:0] \总周期数 , \无条件分支数 , \条件分支成功数 ;
  wire [27:0] adder_2_out;
  wire [31:0] adder_1_out, bit_extender_2_out, bit_extender_3_out, demultiplexer_1_out1, EPC, EPC_IN, I_Din,
       IE, IE_IN, INM, INM_IN, LedData, mips_alu_1_result, mips_ram_1_p8, multiplexer_1_out,
       multiplexer_3_out, multiplexer_4_out, multiplexer_5_out, multiplexer_10_out, multiplexer_11_out,
       multiplexer_15_out, multiplexer_16_out, multiplexer_19_out, multiplexer_20_out, O_Din, shifter_1_out,
       TrapAddr;
  wire [31:5] mips_regifile_1_r1_2;
  wire [31:8] adder_2_out_2, mips_regifile_1_r2;

  Button \u_总复位  (.out(RST));
  Button u_Go (.out(Go));
  Clock clock_1 (.out(CLK));
  Button _1 (.out(IR1));
  Button _2 (.out(IR2));
  Button _3 (.out(IR3));
  LED led_1 (.in(W1));
  LED led_2 (.in(W2));
  LED led_3 (.in(W3));
  Multiplexer #(.select(2), .width(32), .enable("false")) multiplexer_1 (
    .in0({adder_2_out_2[31:28], adder_2_out}), .in1(adder_1_out),
    .in2({adder_2_out_2[31:18], rd, adder_2_out_2[12:8], Func, 2'b00}),
    .in3({mips_regifile_1_r1_2, mips_regifile_1_r1}), .out(multiplexer_1_out), .sel(out_2));
  or or_1 (W1, d_ff_4_q[0], d_ff_1_q);
  or or_2 (W2, d_ff_4_q[1], d_ff_2_q);
  or or_3 (W3, d_ff_4_q[2], d_ff_3_q);
  Multiplexer #(.disabled(0), .enable("false")) multiplexer_2 (
    .in0(backupPC), .in1(IE_IN[0]), .out(multiplexer_2_out), .sel(IE_Write));
  Hex_Digit_Display hex_digit_display_1 (.value(LedData[27:24]));  // open: dp
  Hex_Digit_Display hex_digit_display_2 (.value(LedData[31:28]));  // open: dp
  Multiplexer #(.width(32), .enable("false")) multiplexer_3 (
    .in0(multiplexer_1_out), .in1(TrapAddr), .out(multiplexer_3_out), .sel(INT_CLI));
  D_Flip_Flop d_ff_1 (.clk(IR1), .D(1'b1), .Q(d_ff_1_q), .reset(d_ff_4_q[0]));  // open: Qn, preset, en
  D_Flip_Flop d_ff_2 (.clk(IR2), .D(1'b1), .Q(d_ff_2_q), .reset(d_ff_4_q[1]));  // open: Qn, preset, en
  D_Flip_Flop d_ff_3 (.clk(IR3), .D(1'b1), .Q(d_ff_3_q), .reset(d_ff_4_q[2]));  // open: Qn, preset, en
  or or_4 (or_4_out, IE_Write, backupPC);
  or or_5 (or_5_out, RST, INT_CLI);
  Hex_Digit_Display hex_digit_display_3 (.value(LedData[23:20]));  // open: dp
  Hex_Digit_Display hex_digit_display_4 (.value(LedData[19:16]));  // open: dp
  or or_6 (or_6_out, INT_SIG, not_1_out);
  Multiplexer #(.width(32), .enable("false")) multiplexer_4 (
    .in0(multiplexer_3_out), .in1(EPC), .out(multiplexer_4_out), .sel(backupPC));
  or or_7 (or_7_out, d_ff_1_q, d_ff_4_q[0]);
  or or_8 (or_8_out, d_ff_2_q, d_ff_4_q[1]);
  or or_9 (or_9_out, d_ff_3_q, d_ff_4_q[2]);
  Bit_Extender #(.in_width(32), .out_width(1)) bit_extender_1 (.in(IE), .out(bit_extender_1_out));
  Register #(.width(1)) u_IE (.D(multiplexer_2_out), .en(or_4_out), .Q(bit_extender_1_out), .clk(CLK), .clr(or_5_out));
  Hex_Digit_Display hex_digit_display_5 (.value(LedData[15:12]));  // open: dp
  Hex_Digit_Display hex_digit_display_6 (.value(LedData[11:8]));  // open: dp
  Register #(.width(32)) PC (.D(multiplexer_4_out), .en(or_6_out), .Q(out_1), .clk(CLK), .clr(RST));
  and and_1 (and_1_out, or_7_out, ~INT1_CLR);  // AND_Gate
  and and_2 (and_2_out, or_8_out, ~INT2_CLR);  // AND_Gate
  and and_3 (and_3_out, or_9_out, ~INT3_CLR);  // AND_Gate
  Hex_Digit_Display hex_digit_display_7 (.value(LedData[7:4]));  // open: dp
  Hex_Digit_Display hex_digit_display_8 (.value(LedData[3:0]));  // open: dp
  Adder #(.width(32)) adder_1 (
    .a(shifter_1_out), .b({adder_2_out_2[31:28], adder_2_out}), .out(adder_1_out));  // open: cin, cout
  D_Flip_Flop d_ff_4 (.clk(CLK), .D(and_1_out), .Q(d_ff_4_q[0]));  // open: Qn, preset, en, reset
  D_Flip_Flop d_ff_5 (.clk(CLK), .D(and_2_out), .Q(d_ff_4_q[1]));  // open: Qn, preset, en, reset
  D_Flip_Flop d_ff_6 (.clk(CLK), .D(and_3_out), .Q(d_ff_4_q[2]));  // open: Qn, preset, en, reset
  Multiplexer #(.width(32), .disabled(0), .enable("false")) multiplexer_5 (
    .in0(out_1), .in1(EPC_IN), .out(multiplexer_5_out), .sel(EPC_Write));
  and and_4 (INT_SIG, bit_extender_1_out, INT_FLG);
  Counter #(.width(16), .max('hffff)) counter_1 (
    .count(not_1_out), .Q(\总周期数 ), .clk(CLK), .clr(RST));  // open: load, D, carry
  or or_10 (or_10_out, EPC_Write, INT_CLI);
  ROM #(.addrWidth(10), .dataWidth(32)) rom_1 (
    .addr(out_1[11:2]), .data({Op, adder_2_out_2[27:18], rd, adder_2_out_2[12:8], Func}));  // open: sel
  Adder #(.width(32)) adder_2 (.a(out_1), .b(32'h4), .out({adder_2_out_2[31:28], adder_2_out}));  // open: cin, cout
  Shifter #(.width(32)) shifter_1 (.in(multiplexer_10_out), .\dist (5'b00010), .out(shifter_1_out));
  Register #(.width(32)) u_INM (.D(INM_IN), .en(INM_write), .Q(INM), .clk(CLK), .clr(RST));
  Register #(.width(32)) u_EPC (.D(multiplexer_5_out), .en(or_10_out), .Q(EPC), .clk(CLK), .clr(RST));
  // Probe on \总周期数 
  // Probe on \无条件分支数 
  // Probe on \条件分支成功数 
  // MIPS_Probe mips_probe_1: pin names not known; wires that end beside it: {Op, adder_2_out_2[27:18], rd, adder_2_out_2[12:8], Func}
  assign and_5_out = d_ff_4_q & ~INM[2:0];  // AND_Gate and_5, 3 bits wide
  Comparator #(.width(6)) comparator_1 (.a(6'b010000), .b(Op), .eq(comparator_1_eq));  // open: gt, lt
  Multiplexer #(.width(5), .enable("false")) multiplexer_6 (
    .in0(adder_2_out_2[22:18]), .in1(rd), .out(multiplexer_6_out), .sel(RegDst));
  Multiplexer #(.width(5), .enable("false")) multiplexer_7 (
    .in0(multiplexer_6_out), .in1({5{1'b1}}), .out(out_4), .sel(JAL));
  assign bit_extender_2_out = {{16{rd[4]}}, {rd, adder_2_out_2[12:8], Func}};  // Bit_Extender bit_extender_2
  assign bit_extender_3_out = {{16{1'b0}}, {rd, adder_2_out_2[12:8], Func}};  // Bit_Extender bit_extender_3
  and and_6 (and_6_out, ~register_1_q, INT_SIG);  // AND_Gate
  not not_1 (not_1_out, register_2_q);
  and and_7 (MFC0, comparator_1_eq, comparator_2_eq);
  and and_8 (MTC0, comparator_1_eq, comparator_3_eq);
  Comparator #(.width(5)) comparator_2 (.a(adder_2_out_2[27:23]), .b({5{1'b0}}), .eq(comparator_2_eq));  // open: gt, lt
  Comparator #(.width(5)) comparator_3 (.a(adder_2_out_2[27:23]), .b(5'b00100), .eq(comparator_3_eq));  // open: gt, lt
  Multiplexer #(.width(5), .enable("false")) multiplexer_8 (
    .in0(adder_2_out_2[27:23]), .in1(5'b00010), .out(multiplexer_8_out), .sel(Syscall));
  Multiplexer #(.width(5), .enable("false")) multiplexer_9 (
    .in0(adder_2_out_2[22:18]), .in1(5'b00100), .out(multiplexer_9_out), .sel(Syscall));
  Priority_Encoder #(.select(2), .disabled(0)) priority_encoder_1 (
    .in0(and_5_out[0]), .in1(and_5_out[1]), .in2(and_5_out[2]), .in3(1'b0), .out(priority_encoder_1_out),
    .gs(INT_FLG), .en_in(1'b1));  // open: en_out
  Register #(.width(1)) register_1 (.D(and_6_out), .en(xnor_1_out), .Q(register_1_q), .clk(CLK));  // open: clr
  Register #(.width(1)) register_2 (.D(1'b1), .en(and_9_out), .Q(register_2_q), .clk(CLK), .clr(or_11_out));
  or or_11 (or_11_out, RST, Go);
  and and_9 (and_9_out, Syscall, ~comparator_4_eq);  // AND_Gate
  or or_12 (or_12_out, MFC0, RegWrite);
  Multiplexer #(.width(32), .enable("false")) multiplexer_10 (
    .in0(bit_extender_3_out), .in1(bit_extender_2_out), .out(multiplexer_10_out), .sel(SignedExt));
  Register #(.width(2)) register_3 (.D(priority_encoder_1_out), .en(INT_FLG), .Q(register_3_q), .clk(CLK), .clr(RST));
  and and_10 (\INT脉冲 , and_6_out, ~register_1_q);  // AND_Gate
  Comparator #(.width(32)) comparator_4 (
    .a(32'h22), .b({mips_regifile_1_r1_2, mips_regifile_1_r1}), .eq(comparator_4_eq));  // open: gt, lt
  MIPS_Regifile mips_regifile_1 (
    .Din(O_Din), .Clk(CLK), .R1({mips_regifile_1_r1_2, mips_regifile_1_r1}),
    .R2({mips_regifile_1_r2, mips_regifile_1_r2_2}), .WE(or_12_out), .W_num(out_4),
    .R1_num(multiplexer_8_out), .R2_num(multiplexer_9_out));
  Multiplexer #(.width(32), .disabled(0), .enable("false")) multiplexer_11 (
    .in0({mips_regifile_1_r2, mips_regifile_1_r2_2}), .in1(multiplexer_10_out), .out(multiplexer_11_out),
    .sel(AluSrcB));
  Multiplexer #(.select(2), .width(32), .enable("false")) multiplexer_12 (
    .in0(32'h3048), .in1(32'h3150), .in2(32'h3258), .out(TrapAddr), .sel(priority_encoder_1_out));  // open: in3
  Register #(.width(1)) register_4 (.D(register_1_q), .en(xnor_1_out), .Q(INT_CLI), .clk(CLK));  // open: clr
  and and_11 (and_11_out, comparator_4_eq, Syscall);
  Decoder #(.select(2), .disabled(0)) decoder_1 (
    .out0(INT1_CLR), .out1(INT2_CLR), .out2(INT3_CLR), .sel(register_3_q), .en(ERET));  // open: out3
  Register #(.width(32)) register_5 (
    .D({mips_regifile_1_r2, mips_regifile_1_r2_2}), .en(and_11_out), .Q(LedData), .clk(CLK), .clr(RST));
  Multiplexer #(.width(5), .enable("false")) multiplexer_13 (
    .in0(mips_regifile_1_r1), .in1(adder_2_out_2[12:8]), .out(multiplexer_13_out), .sel(Shamt));
  Multiplexer #(.enable("false")) multiplexer_14 (.in0(INT_CLI), .in1(INT_FLG), .out(multiplexer_14_out), .sel(ERET));
  \硬布线控制器  \u_硬布线控制器_1  (
    .Func(Func), .OP(Op), .ALU_OP(out_3), .MemToReg(MemToReg), .MemWrite(MemWrite), .ALU_SRC(AluSrcB),
    .RegWrite(RegWrite), .SysCALL(Syscall), .SignedExt(SignedExt), .RegDst(RegDst), .JR(JR), .JMP(JMP),
    .Beq(Beq), .Bne(Bne), .JAL(JAL), .SHAMT(Shamt), .SB(SB), .BGTZ(BGTZ));
  MIPS_ALU mips_alu_1 (
    .X({mips_regifile_1_r1_2, mips_regifile_1_r1}), .Y(multiplexer_11_out), .AluOP(out_3),
    .Equal(mips_alu_1_equal), .Result(mips_alu_1_result), .shamt(multiplexer_13_out));  // open: Result_2
  Decoder #(.select(2), .enable("false")) decoder_2 (
    .out0(decoder_2_out0[0]), .out1(decoder_2_out0[1]), .out2(decoder_2_out0[2]), .out3(decoder_2_out0[3]),
    .sel(mips_alu_1_result[1:0]));
  Comparator #(.width(32)) comparator_5 (
    .a({mips_regifile_1_r1_2, mips_regifile_1_r1}), .b({32{1'b0}}), .gt(comparator_5_gt));  // open: eq, lt
  Register #(.width(1)) register_6 (
    .D(multiplexer_14_out), .en(xnor_1_out), .Q(register_6_q), .clk(CLK), .clr(or_16_out));
  xnor xnor_1 (xnor_1_out, register_6_q, ERET);
  not not_2 (not_2_out, mips_alu_1_equal);
  and and_12 (and_12_out, not_2_out, Bne);
  and and_13 (and_13_out, mips_alu_1_equal, Beq);
  Multiplexer #(.width(32), .enable("false")) multiplexer_15 (
    .in0({mips_regifile_1_r2, mips_regifile_1_r2_2}),
    .in1({mips_regifile_1_r2_2, mips_regifile_1_r2_2, mips_regifile_1_r2_2, mips_regifile_1_r2_2}),
    .out(multiplexer_15_out), .sel(SB));
  and and_14 (and_14_out, comparator_5_gt, BGTZ);
  Multiplexer #(.select(2), .width(32), .enable("false")) multiplexer_16 (
    .in0(IE), .in1(EPC), .in2(INM), .out(multiplexer_16_out), .sel(rd[1:0]));  // open: in3
  Multiplexer #(.width(4), .enable("false")) multiplexer_17 (
    .in0(4'b1111), .in1(decoder_2_out0), .out(multiplexer_17_out), .sel(SB));
  Multiplexer #(.enable("false")) multiplexer_18 (
    .in0(register_6_q), .in1(1'b0), .out(multiplexer_18_out), .sel(backupPC));
  or or_13 (or_13_out, xnor_1_out, backupPC);
  Counter #(.width(16), .max('hffff)) counter_2 (
    .count(and_15_out), .Q(\无条件分支数 ), .clk(CLK), .clr(RST));  // open: load, D, carry
  and and_15 (and_15_out, not_1_out, out_2[1]);
  or or_14 (out_2[1], JAL, JMP, JR);
  // MIPS_RAM mips_ram_1: pin names not known; wires that end beside it: mips_alu_1_result[25:2], multiplexer_15_out, MemWrite, multiplexer_17_out, CLK, 1'b1, RST, mips_ram_1_p8
  Demultiplexer #(.width(32), .enable("false")) demultiplexer_1 (
    .out0(O_Din), .out1(demultiplexer_1_out1), .in(multiplexer_19_out), .sel(MTC0));
  Multiplexer #(.width(32), .enable("false")) multiplexer_19 (
    .in0(I_Din), .in1(multiplexer_16_out), .out(multiplexer_19_out), .sel(MFC0));
  Register #(.width(1)) register_7 (.D(multiplexer_18_out), .en(or_13_out), .Q(backupPC), .clk(CLK), .clr(or_16_out));
  \中断信号生成  \u_中断信号生成_1  (
    .OP0(Op[0]), .OP1(Op[1]), .OP2(Op[2]), .OP3(Op[3]), .OP4(Op[4]), .OP5(Op[5]), .F0(Func[0]), .F1(Func[1]),
    .F2(Func[2]), .F3(Func[3]), .F4(Func[4]), .F5(Func[5]), .ERET(ERET));
  or or_15 (out_2[0], JR, and_12_out, and_13_out, and_14_out);
  Multiplexer #(.width(32), .enable("false")) multiplexer_20 (
    .in0(mips_alu_1_result), .in1(mips_ram_1_p8), .out(multiplexer_20_out), .sel(MemToReg));
  Decoder #(.select(2), .disabled(0)) decoder_3 (
    .out0(IE_Write), .out1(EPC_Write), .out2(INM_write), .sel(rd[1:0]), .en(MTC0));  // open: out3
  or or_16 (or_16_out, RST, \INT脉冲 );
  Counter #(.width(16), .max('hffff)) counter_3 (
    .count(and_16_out), .Q(\条件分支成功数 ), .clk(CLK), .clr(RST));  // open: load, D, carry
  and and_16 (and_16_out, not_1_out, or_17_out);
  or or_17 (or_17_out, and_12_out, and_13_out, and_14_out);
  Multiplexer #(.width(32), .enable("false")) multiplexer_21 (
    .in0(multiplexer_20_out), .in1({adder_2_out_2[31:28], adder_2_out}), .out(I_Din), .sel(JAL));
  Demultiplexer #(.select(2), .width(32), .enable("false")) demultiplexer_2 (
    .out0(IE_IN), .out1(EPC_IN), .out2(INM_IN), .in(demultiplexer_1_out1), .sel(rd[1:0]));  // open: out3

  // Other names for the same wires on the sheet: AluOP[3:0] = out_3; PC[31:0] = out_1; PCSrc[1:0] = out_2

  // Notes on the sheet:
  //   中断源
  //   中断等待指示
  //   数码管输出
  //   指令存储器
  //   contents of rom_1 (hex, n*v repeats v):
  //   40090000 20090001 40890000 201d0200 20090000 40891000 20100001 20130000 20080008 20090001 139900
  //   2709825 132020 20020022 c 1094022 1500fff9 8000c06 0 23bdfffc afbd0000 401f0800 23bdfffc afbf0000
  //   401f1000 23bdfffc afbf0000 23bdfffc afb00000 23bdfffc afb30000 23bdfffc afb40000 23bdfffc afb50000
  //   23bdfffc afb60000 23bdfffc afa20000 23bdfffc afa90000 201f0001 409f1000 40090000 20090001 40890000
  //   20160001 20140006 20150001 168020 108100 2149825 132020 20020022 c 1600fffa 295a022 1680fff7
  //   40090000 20090000 40890000 8fa90000 27bd0004 8fa20000 27bd0004 8fb60000 27bd0004 8fb50000 27bd0004
  //   8fb40000 27bd0004 8fb30000 27bd0004 8fb00000 27bd0004 8fbf0000 27bd0004 409f1000 8fbf0000 27bd0004
  //   409f0800 8fbd0000 27bd0004 42000018 0 23bdfffc afbd0000 401f0800 23bdfffc afbf0000 401f1000 23bdfffc
  //   afbf0000 23bdfffc afb00000 23bdfffc afb30000 23bdfffc afb40000 23bdfffc afb50000 23bdfffc afb60000
  //   23bdfffc afa20000 23bdfffc afa90000 201f0003 409f1000 40090000 20090001 40890000 20160002 20140006
  //   20150001 168020 108100 2149825 132020 20020022 c 1600fffa 295a022 1680fff7 40090000 20090000
  //   40890000 8fa90000 27bd0004 8fa20000 27bd0004 8fb60000 27bd0004 8fb50000 27bd0004 8fb40000 27bd0004
  //   8fb30000 27bd0004 8fb00000 27bd0004 8fbf0000 27bd0004 409f1000 8fbf0000 27bd0004 409f0800 8fbd0000
  //   27bd0004 42000018 0 23bdfffc afbd0000 401f0800 23bdfffc afbf0000 401f1000 23bdfffc afbf0000 23bdfffc
  //   afb00000 23bdfffc afb30000 23bdfffc afb40000 23bdfffc afb50000 23bdfffc afb60000 23bdfffc afa20000
  //   23bdfffc afa90000 201f0007 409f1000 40090000 20090001 40890000 20160003 20140006 20150001 168020
  //   108100 2149825 132020 20020022 c 1600fffa 295a022 1680fff7 40090000 20090000 40890000 8fa90000
  //   27bd0004 8fa20000 27bd0004 8fb60000 27bd0004 8fb50000 27bd0004 8fb40000 27bd0004 8fb30000 27bd0004
  //   8fb00000 27bd0004 8fbf0000 27bd0004 409f1000 8fbf0000 27bd0004 409f0800 8fbd0000 27bd0004 42000018
  //   OP
  //   Func
  //   rs
  //   指令字
  //   rt
  //   rd
endmodule

module \中断信号生成  (
  input  OP0,
  input  OP1,
  input  OP2,
  input  OP3,
  input  OP4,
  input  OP5,
  input  F0,
  input  F1,
  input  F2,
  input  F3,
  input  F4,
  input  F5,
  output ERET
);

  wire not_1_out, not_2_out, not_3_out, not_4_out, not_5_out, not_6_out, not_7_out, not_8_out, not_9_out;

  not not_1 (not_1_out, OP5);
  not not_2 (not_2_out, OP3);
  not not_3 (not_3_out, OP2);
  not not_4 (not_4_out, OP1);
  not not_5 (not_5_out, OP0);
  not not_6 (not_6_out, F5);
  not not_7 (not_7_out, F2);
  not not_8 (not_8_out, F1);
  not not_9 (not_9_out, F0);
  and and_1 (ERET, not_1_out, OP4, not_2_out, not_3_out, not_4_out, not_5_out, not_6_out, F4, F3, not_7_out, not_8_out, not_9_out);
endmodule
